// Logisim project 三输入多数表决器.circ as structural Verilog: 1 circuit, main circuit main
module main (
  input  X,
  input  Y,
  input  Z,
  output out_4
);

  wire AND1_out, AND2_out, AND3_out;

  and AND1 (AND1_out, X, Z);
  and AND2 (AND2_out, X, Y);
  and AND3 (AND3_out, Z, Y);
  or OR1 (out_4, AND1_out, AND2_out, AND3_out);

  // Notes on the sheet:
  //   多数表决器
endmodule
