// Logisim project 奇偶校验电路.circ as structural Verilog: 2 circuits, main circuit main
module main (
  input  N0,
  input  N1,
  input  N2,
  input  N3,
  output EVEN,
  output ODD
);

  wire xor_1_out, xor_2_out;

  xor xor_1 (xor_1_out, N0, N1);
  xor xor_2 (xor_2_out, N2, N3);
  xor xor_3 (EVEN, xor_1_out, xor_2_out);
  not not_1 (ODD, EVEN);

  // Notes on the sheet:
  //   4位奇偶校验电路
endmodule

module _12 (
  input  N0,
  input  N1,
  input  N2,
  input  N3,
  output EVEN,
  output ODD
);

  wire and_1_out, and_2_out, and_3_out, and_4_out, and_5_out, and_6_out, and_7_out, and_8_out, and_9_out,
       and_10_out, and_11_out, and_12_out, and_13_out, and_14_out, and_15_out, and_16_out, not_1_out,
       not_2_out, not_3_out, not_4_out, not_5_out, not_6_out, not_7_out, not_8_out, not_9_out, not_10_out,
       not_11_out, not_12_out, not_13_out, not_14_out, not_15_out, not_16_out, not_17_out, not_18_out,
       not_19_out, not_20_out, not_21_out, not_22_out, not_23_out, not_24_out, not_25_out, not_26_out,
       not_27_out, not_28_out, not_29_out, not_30_out, not_31_out, not_32_out;

  not not_1 (not_1_out, N0);
  not not_2 (not_2_out, N1);
  not not_3 (not_3_out, N2);
  not not_4 (not_4_out, N0);
  not not_5 (not_5_out, N1);
  not not_6 (not_6_out, N3);
  not not_7 (not_7_out, N0);
  not not_8 (not_8_out, N2);
  not not_9 (not_9_out, N3);
  not not_10 (not_10_out, N0);
  not not_11 (not_11_out, N1);
  not not_12 (not_12_out, N2);
  not not_13 (not_13_out, N3);
  not not_14 (not_14_out, N1);
  not not_15 (not_15_out, N2);
  not not_16 (not_16_out, N3);
  not not_17 (not_17_out, N0);
  not not_18 (not_18_out, N1);
  not not_19 (not_19_out, N2);
  not not_20 (not_20_out, N3);
  not not_21 (not_21_out, N0);
  not not_22 (not_22_out, N1);
  not not_23 (not_23_out, N0);
  not not_24 (not_24_out, N2);
  not not_25 (not_25_out, N0);
  not not_26 (not_26_out, N3);
  not not_27 (not_27_out, N1);
  not not_28 (not_28_out, N2);
  not not_29 (not_29_out, N1);
  not not_30 (not_30_out, N3);
  not not_31 (not_31_out, N2);
  not not_32 (not_32_out, N3);
  and and_1 (and_1_out, not_1_out, not_2_out, not_3_out, N3);
  and and_2 (and_2_out, not_4_out, not_5_out, N2, not_6_out);
  and and_3 (and_3_out, not_7_out, N1, not_8_out, not_9_out);
  and and_4 (and_4_out, not_10_out, N1, N2, N3);
  and and_5 (and_5_out, N0, not_11_out, not_12_out, not_13_out);
  and and_6 (and_6_out, N0, not_14_out, N2, N3);
  and and_7 (and_7_out, N0, N1, not_15_out, N3);
  and and_8 (and_8_out, N0, N1, N2, not_16_out);
  and and_9 (and_9_out, not_17_out, not_18_out, not_19_out, not_20_out);
  and and_10 (and_10_out, not_21_out, not_22_out, N2, N3);
  and and_11 (and_11_out, not_23_out, N1, not_24_out, N3);
  and and_12 (and_12_out, not_25_out, N1, N2, not_26_out);
  and and_13 (and_13_out, N0, not_27_out, not_28_out, N3);
  and and_14 (and_14_out, N0, not_29_out, N2, not_30_out);
  and and_15 (and_15_out, N0, N1, not_31_out, not_32_out);
  and and_16 (and_16_out, N0, N1, N2, N3);
  or or_1 (EVEN, and_1_out, and_2_out, and_3_out, and_4_out, and_5_out, and_6_out, and_7_out, and_8_out);
  or or_2 (ODD, and_9_out, and_10_out, and_11_out, and_12_out, and_13_out, and_14_out, and_15_out, and_16_out);
endmodule
