// Logisim project lab2-1.circ as structural Verilog: 1 circuit, main circuit main
module main (
  input  s1,
  input  s2_prime,
  input  s3_prime,
  input  a0,
  input  a1,
  input  a2,
  output y0_prime,
  output y1_prime,
  output y2_prime,
  output y3,
  output y4_prime,
  output y5_prime,
  output y6_prime,
  output y7_prime
);

  wire g0_out, g1_out, g2_out, g3_out, g4_out, g5_out, g6_out, g7_out, not_1_out, not_2_out, not_3_out,
       not_4_out, not_5_out, not_6_out, not_7_out, not_8_out, S_out;

  not not_1 (not_1_out, s2_prime);
  not not_2 (not_2_out, s3_prime);
  not not_3 (not_3_out, a0);
  not not_4 (not_4_out, a1);
  not not_5 (not_5_out, a2);
  and S (S_out, s1, not_1_out, not_2_out);
  not not_6 (not_6_out, not_3_out);
  not not_7 (not_7_out, not_4_out);
  not not_8 (not_8_out, not_5_out);
  and g0 (g0_out, not_3_out, not_4_out, not_5_out, S_out);
  not not_9 (y1_prime, g1_out);
  and g1 (g1_out, not_4_out, not_5_out, not_6_out, S_out);
  and g2 (g2_out, not_3_out, not_5_out, not_7_out, S_out);
  and g3 (g3_out, not_5_out, not_6_out, not_7_out, S_out);
  not not_10 (y4_prime, g4_out);
  and g4 (g4_out, not_3_out, not_4_out, not_8_out, S_out);
  and g5 (g5_out, not_4_out, not_6_out, not_8_out, S_out);
  not not_11 (y5_prime, g5_out);
  not not_12 (y6_prime, g6_out);
  and g6 (g6_out, not_3_out, not_7_out, not_8_out, S_out);
  not not_13 (y7_prime, g7_out);
  and g7 (g7_out, S_out, not_7_out, not_8_out, not_6_out);
  not not_14 (y0_prime, g0_out);
  not not_15 (y2_prime, g2_out);
  not not_16 (y3, g3_out);

  // Notes on the sheet:
  //   3-8译码器
endmodule
