// Logisim project lab2-4.circ as structural Verilog: 2 circuits, main circuit main
module main (
  input  D0,
  input  D1,
  input  S,
  output Y
);

  wire transistor_1_out;

  Transistor transistor_1 (.in(1'b1), .out(transistor_1_out), .gate(S));
  Transistor #(.\type ("n")) transistor_2 (.in(1'b0), .out(transistor_1_out), .gate(S));
  // Transmission_Gate transmission_1: pin names not known; wires that end beside it: D0, S, transistor_1_out, Y
  // Transmission_Gate transmission_2: pin names not known; wires that end beside it: D1, transistor_1_out, S, Y

  // Notes on the sheet:
  //   2选1多路选择器
endmodule

module lab2_4 (
  input  in_1,
  input  S3,
  input  S2,
  input  S1,
  input  A,
  input  B,
  output out_7,
  output C
);

  wire _2_1MUX_2_y, _2_1MUX_3_y, _2_1MUX_4_y, _2_1MUX_5_y, _2_1MUX_6_y, _2_1MUX_y, adder_1_out, and_1_out,
       and_2_out, B_out, not_1_out, not_2_out, not_3_out, or_1_out, subtractor_1_out, xnor_1_out;

  Adder #(.width(1)) adder_1 (.a(A), .b(B), .out(adder_1_out), .cin(in_1), .cout(out_7));
  not not_1 (not_1_out, A);
  or or_1 (or_1_out, A, B);
  xnor xnor_1 (xnor_1_out, A, B);
  and u_B (B_out, A, B);
  Subtractor #(.width(1)) subtractor_1 (.a(A), .b(B), .out(subtractor_1_out));  // open: bin, bout
  not not_2 (not_2_out, B);
  main _2_1MUX (.D0(adder_1_out), .D1(xnor_1_out), .S(S3), .Y(_2_1MUX_y));
  main _2_1MUX_2 (.D0(B_out), .D1(A), .S(S3), .Y(_2_1MUX_2_y));
  main _2_1MUX_3 (.D0(subtractor_1_out), .D1(not_1_out), .S(S3), .Y(_2_1MUX_3_y));
  main _2_1MUX_4 (.D0(or_1_out), .D1(not_2_out), .S(S3), .Y(_2_1MUX_4_y));
  not not_3 (not_3_out, S1);
  main _2_1MUX_5 (.D0(_2_1MUX_y), .D1(_2_1MUX_2_y), .S(S2), .Y(_2_1MUX_5_y));
  main _2_1MUX_6 (.D0(_2_1MUX_3_y), .D1(_2_1MUX_4_y), .S(S2), .Y(_2_1MUX_6_y));
  and and_1 (and_1_out, not_3_out, _2_1MUX_5_y);
  and and_2 (and_2_out, S1, _2_1MUX_6_y);
  or or_2 (C, and_1_out, and_2_out);

  // Notes on the sheet:
  //   或
  //   异或非
  //   A非
endmodule
