// Logisim project LAB3-2.circ as structural Verilog: 2 circuits, main circuit SHRG4U
module SHRG4U (
  input  CLK,
  input  in_2,
  input  LIN,
  input  D,
  input  C,
  input  B,
  input  S1,
  input  S0,
  input  A,
  input  RIN,
  output out_11,
  output out_12,
  output out_13,
  output out_14
);

  wire and_1_out, and_2_out, and_3_out, and_4_out, and_5_out, and_6_out, and_7_out, and_8_out, and_9_out,
       and_10_out, and_11_out, and_12_out, and_13_out, and_14_out, and_15_out, and_16_out, not_1_out,
       not_2_out, not_3_out, not_4_out, or_1_out, or_2_out, or_3_out, or_4_out;

  not not_1 (not_1_out, S1);
  not not_2 (not_2_out, S0);
  not not_3 (not_3_out, CLK);
  not not_4 (not_4_out, in_2);
  and and_1 (and_1_out, not_4_out, LIN, S1, not_2_out);
  and and_2 (and_2_out, not_4_out, not_2_out, not_1_out, out_11);
  and and_3 (and_3_out, not_4_out, S1, S0, D);
  and and_4 (and_4_out, not_4_out, not_1_out, S0, out_12);
  and and_5 (and_5_out, not_4_out, S1, not_2_out, out_11);
  and and_6 (and_6_out, not_4_out, not_2_out, not_1_out, out_12);
  and and_7 (and_7_out, not_4_out, S1, S0, C);
  and and_8 (and_8_out, not_4_out, not_1_out, S0, out_13);
  and and_9 (and_9_out, not_4_out, S1, not_2_out, out_12);
  and and_10 (and_10_out, not_4_out, not_2_out, not_1_out, out_13);
  and and_11 (and_11_out, not_4_out, S1, S0, B);
  and and_12 (and_12_out, not_4_out, not_1_out, S0, out_14);
  and and_13 (and_13_out, not_4_out, S1, not_2_out, out_13);
  and and_14 (and_14_out, not_4_out, not_2_out, not_1_out, out_14);
  and and_15 (and_15_out, not_4_out, S1, S0, A);
  and and_16 (and_16_out, not_4_out, not_1_out, S0, RIN);
  or or_1 (or_1_out, and_5_out, and_6_out, and_7_out, and_8_out);
  or or_2 (or_2_out, and_9_out, and_10_out, and_11_out, and_12_out);
  or or_3 (or_3_out, and_13_out, and_14_out, and_15_out, and_16_out);
  or or_4 (or_4_out, and_1_out, and_2_out, and_3_out, and_4_out);
  D_Flip_Flop d_ff_1 (.clk(not_3_out), .D(or_4_out), .Q(out_11));  // open: Qn, preset, reset
  D_Flip_Flop d_ff_2 (.clk(not_3_out), .D(or_1_out), .Q(out_12));  // open: Qn, preset, reset
  D_Flip_Flop d_ff_3 (.clk(not_3_out), .D(or_2_out), .Q(out_13));  // open: Qn, preset, reset
  D_Flip_Flop d_ff_4 (.clk(not_3_out), .D(or_3_out), .Q(out_14));  // open: Qn, preset, reset

  // Notes on the sheet:
  //   CLR
  //   1
endmodule

module \右移  (
  input  in_1,
  input  in_2,
  input  in_3,
  input  in_4,
  input  in_5,
  input  in_6,
  input  in_7,
  input  in_8,
  input  in_9,
  output out_10,
  output out_11,
  output out_12,
  output out_13
);

  wire and_1_out, and_2_out, clock_1_out, not_1_out, not_2_out, or_1_out, or_2_out;

  Clock clock_1 (.out(clock_1_out));
  SHRG4U shrg4u_1 (
    .CLK(clock_1_out), .in_2(in_1), .LIN(in_2), .D(in_3), .C(in_4), .B(in_5), .S1(in_7), .S0(in_8), .A(in_6),
    .RIN(or_1_out), .out_11(out_10), .out_12(out_11), .out_13(out_12), .out_14(out_13));
  not not_1 (not_1_out, out_11);
  not not_2 (not_2_out, out_10);
  // Digital_Oscilloscope #(.nState(16)) digital_oscilloscope_1: pin names not known; wires that end beside it: clock_1_out, out_13, out_12
  and and_1 (and_1_out, not_1_out, out_10);
  and and_2 (and_2_out, out_11, not_2_out);
  or or_1 (or_1_out, in_9, or_2_out);
  or or_2 (or_2_out, and_1_out, and_2_out);
  Hex_Digit_Display hex_digit_display_1 (.value({out_10, out_11, out_12, out_13}), .dp(1'b1));
endmodule
