// Logisim project LAB 5-1.circ as structural Verilog: 1 circuit, main circuit main
module main (
  input  [11:0] \地址数据 ,
  input  [31:0] \输入数据 ,
  input  \输入使能 ,
  input  \片选 ,
  input  \输出使能 ,
  input  [11:0] \地址数据_2 ,
  input  [7:0] \输入数据_2 ,
  input  \输入使能_2 ,
  input  \片选_2 ,
  input  \输出使能_2 ,
  output [31:0] out_11
);

  wire \复位按钮_2_out , \复位按钮_out , \时钟信号_2_out , \时钟信号_out ;
  wire [7:0] \存储器RAM_data ;

  Clock \u_时钟信号  (.out(\时钟信号_out ));
  Button \u_复位按钮  (.out(\复位按钮_out ));
  Clock \u_时钟信号_2  (.out(\时钟信号_2_out ));
  Button \u_复位按钮_2  (.out(\复位按钮_2_out ));
  RAM #(.addrWidth(12), .bus("separate"), .Select("low")) \u_存储器RAM  (
    .addr(\地址数据_2 ), .din(\输入数据_2 ), .data(\存储器RAM_data ), .str(\输入使能_2 ), .sel(\片选_2 ), .clk(\时钟信号_2_out ),
    .ld(\输出使能_2 ), .clr(\复位按钮_2_out ));
  RAM #(.addrWidth(12), .dataWidth(32), .bus("separate"), .Select("low")) \u_存储器RAM_2  (
    .addr(\地址数据 ), .din(\输入数据 ), .data(out_11), .str(\输入使能 ), .sel(\片选 ), .clk(\时钟信号_out ), .ld(\输出使能 ),
    .clr(\复位按钮_out ));
  TTY tty_1 (.data(\存储器RAM_data [6:0]), .clk(\时钟信号_2_out ), .clr(\复位按钮_2_out ));  // open: we
endmodule
