// Logisim project LAB 5-2.circ as structural Verilog: 12 circuits, main circuit CLU
module CLU (
  input  C0,
  input  G4,
  input  P4,
  input  G3,
  input  P3,
  input  G2,
  input  P2,
  input  G1,
  input  P1,
  output C4,
  output C3,
  output C2,
  output C1
);

  wire and_1_out, and_2_out, and_3_out, and_4_out, and_5_out, and_6_out, and_7_out, and_8_out, and_9_out,
       and_10_out;

  and and_1 (and_1_out, P4, G3);
  and and_2 (and_2_out, P4, P3, G2);
  or or_1 (C4, G4, and_1_out, and_2_out, and_3_out, and_4_out);
  and and_3 (and_3_out, P4, P3, P2, G1);
  and and_4 (and_4_out, P4, P3, P2, P1, C0);
  or or_2 (C3, G3, and_5_out, and_7_out, and_6_out);
  and and_5 (and_5_out, P3, G2);
  and and_6 (and_6_out, P3, P2, P1, C0);
  and and_7 (and_7_out, P3, P2, G1);
  or or_3 (C2, G2, and_8_out, and_9_out);
  and and_8 (and_8_out, P2, G1);
  and and_9 (and_9_out, P2, P1, C0);
  or or_4 (C1, G1, and_10_out);
  and and_10 (and_10_out, P1, C0);
endmodule

module \全加器  (
  input  A,
  input  B,
  input  C,
  output G,
  output P,
  output F
);

  wire xor_1_out;

  and and_1 (G, A, B);
  or or_1 (P, A, B);
  xor xor_1 (xor_1_out, A, B);
  xor xor_2 (F, xor_1_out, C);
endmodule

module \_4位加法器  (
  input  [3:0] B,
  input  [3:0] A,
  input  C0,
  output Gg,
  output Pg,
  output C4,
  output [3:0] S,
  output F3,
  output C3
);

  wire clu_1_c1, clu_1_c2, FA0_g, FA0_p, FA1_g, FA1_p, FA2_g, FA2_p, FA3_g, FA3_p;

  \全加器  FA3 (.A(A[3]), .B(B[3]), .C(C3), .G(FA3_g), .P(FA3_p), .F(F3));
  \全加器  FA2 (.A(A[2]), .B(B[2]), .C(clu_1_c2), .G(FA2_g), .P(FA2_p), .F(S[2]));
  \全加器  FA1 (.A(A[1]), .B(B[1]), .C(clu_1_c1), .G(FA1_g), .P(FA1_p), .F(S[1]));
  \全加器  FA0 (.A(A[0]), .B(B[0]), .C(C0), .G(FA0_g), .P(FA0_p), .F(S[0]));
  CLU clu_1 (
    .C0(C0), .C4(C4), .C3(C3), .C2(clu_1_c2), .C1(clu_1_c1), .G4(FA3_g), .P4(FA3_p), .G3(FA2_g), .P3(FA2_p),
    .G2(FA1_g), .P2(FA1_p), .G1(FA0_g), .P1(FA0_p));
  \Gg和Pg  \gg和pg_1  (
    .P0(FA0_p), .G0(FA0_g), .P1(FA1_p), .G1(FA1_g), .P2(FA2_p), .G2(FA2_g), .P3(FA3_p), .G3(FA3_g), .Gg(Gg),
    .Pg(Pg));

  assign S[3] = F3;
endmodule

module \Gg和Pg  (
  input  P0,
  input  G0,
  input  P1,
  input  G1,
  input  P2,
  input  G2,
  input  P3,
  input  G3,
  output Gg,
  output Pg
);

  wire and_1_out, and_2_out, and_3_out;

  and and_1 (and_1_out, P3, G2);
  and and_2 (and_2_out, P3, P2, G1);
  and and_3 (and_3_out, P3, P2, P1, G0);
  and and_4 (Pg, P3, P2, P1, P0);
  or or_1 (Gg, G3, and_1_out, and_2_out, and_3_out);
endmodule

module \_16位加法器  (
  input  C0,
  input  [15:0] A,
  input  [15:0] B,
  output C4,
  output Cn_1,
  output [15:0] S,
  output Fn_1
);

  wire clu_1_c1, clu_1_c2, clu_1_c3, \n4位加法器_1_gg , \n4位加法器_1_pg , \n4位加法器_2_gg , \n4位加法器_2_pg ,
       \n4位加法器_3_gg , \n4位加法器_3_pg , \n4位加法器_4_gg , \n4位加法器_4_pg ;

  \_4位加法器  \u_4位加法器_1  (
    .B(B[3:0]), .A(A[3:0]), .Gg(\n4位加法器_1_gg ), .Pg(\n4位加法器_1_pg ), .S(S[3:0]), .C0(C0));  // open: C4, C3, F3
  \_4位加法器  \u_4位加法器_2  (
    .B(B[7:4]), .A(A[7:4]), .Gg(\n4位加法器_2_gg ), .Pg(\n4位加法器_2_pg ), .S(S[7:4]), .C0(clu_1_c1));  // open: C4, C3, F3
  \_4位加法器  \u_4位加法器_3  (
    .B(B[11:8]), .A(A[11:8]), .Gg(\n4位加法器_3_gg ), .Pg(\n4位加法器_3_pg ), .S(S[11:8]), .C0(clu_1_c2));  // open: C4, C3, F3
  \_4位加法器  \u_4位加法器_4  (
    .B(B[15:12]), .A(A[15:12]), .Gg(\n4位加法器_4_gg ), .Pg(\n4位加法器_4_pg ), .C4(C4), .S(S[15:12]), .C0(clu_1_c3),
    .C3(Cn_1), .F3(Fn_1));
  CLU clu_1 (
    .C0(C0), .C3(clu_1_c3), .C2(clu_1_c2), .C1(clu_1_c1), .G4(\n4位加法器_4_gg ), .P4(\n4位加法器_4_pg ),
    .G3(\n4位加法器_3_gg ), .P3(\n4位加法器_3_pg ), .G2(\n4位加法器_2_gg ), .P2(\n4位加法器_2_pg ), .G1(\n4位加法器_1_gg ),
    .P1(\n4位加法器_1_pg ));  // open: C4
endmodule

module \_32位加法器  (
  input  C0,
  input  [31:0] A,
  input  [31:0] B,
  output ZF,
  output CF,
  output [31:0] out_6,
  output OF,
  output SF
);

  wire _0_15_c4, _16_31_c4, _16_31_cn_1, or_1_out;

  \_16位加法器  _0_15 (.C0(C0), .A(A[15:0]), .B(B[15:0]), .C4(_0_15_c4), .S(out_6[15:0]));  // open: Cn_1, Fn_1
  \_16位加法器  _16_31 (
    .C0(_0_15_c4), .A(A[31:16]), .B(B[31:16]), .C4(_16_31_c4), .Cn_1(_16_31_cn_1), .S(out_6[31:16]), .Fn_1(SF));
  xor xor_1 (CF, C0, _16_31_c4);
  xor xor_2 (OF, _16_31_c4, _16_31_cn_1);
  not not_1 (ZF, or_1_out);
  or or_1 (or_1_out, out_6[0], out_6[1], out_6[2], out_6[3], out_6[4], out_6[5], out_6[6], out_6[7], out_6[8], out_6[9], out_6[10], out_6[11], out_6[12], out_6[13], out_6[14], out_6[15], out_6[16], out_6[17], out_6[18], out_6[19], out_6[20], out_6[21], out_6[22], out_6[23], out_6[24], out_6[25], out_6[26], out_6[27], out_6[28], out_6[29], out_6[30], out_6[31]);
endmodule

module ALUCtr (
  input  [3:0] Cin,
  output SUBctr,
  output SIGctr,
  output [1:0] OPctr
);

  wire and_1_out, not_2_out, not_3_out;

  or or_1 (SUBctr, Cin[1], Cin[3]);
  not not_1 (SIGctr, Cin[0]);
  not not_2 (not_2_out, Cin[2]);
  not not_3 (not_3_out, Cin[3]);
  and and_1 (and_1_out, not_2_out, Cin[1]);
  and and_2 (OPctr[0], not_3_out, Cin[1]);
  or or_2 (OPctr[1], Cin[0], and_1_out);
endmodule

module ALU (
  input  [3:0] ALUctr,
  input  [31:0] A,
  input  [31:0] B,
  output Zero,
  output [31:0] Result
);

  wire aluctr_1_sigctr, aluctr_1_subctr, multiplexer_2_out, \n32位加法器_1_cf , \n32位加法器_1_of , \n32位加法器_1_sf ,
       xor_2_out, xor_3_out;
  wire [1:0] aluctr_1_opctr;
  wire [31:0] bit_extender_1_out, bit_extender_2_out, \n32位加法器_1_out_6 , or_1_out, xor_1_out;

  assign bit_extender_1_out = {{31{aluctr_1_subctr}}, aluctr_1_subctr};  // Bit_Extender bit_extender_1
  assign or_1_out = A | B;  // OR_Gate or_1, 32 bits wide
  assign xor_1_out = B ^ bit_extender_1_out;  // XOR_Gate xor_1, 32 bits wide
  \_32位加法器  \u_32位加法器_1  (
    .C0(aluctr_1_subctr), .A(A), .B(xor_1_out), .ZF(Zero), .CF(\n32位加法器_1_cf ), .out_6(\n32位加法器_1_out_6 ),
    .OF(\n32位加法器_1_of ), .SF(\n32位加法器_1_sf ));
  xor xor_2 (xor_2_out, aluctr_1_subctr, \n32位加法器_1_cf );
  xor xor_3 (xor_3_out, \n32位加法器_1_of , \n32位加法器_1_sf );
  Multiplexer #(.select(2), .width(32), .enable("false")) multiplexer_1 (
    .in0(\n32位加法器_1_out_6 ), .in1(or_1_out), .in2(B), .in3(bit_extender_2_out), .out(Result),
    .sel(aluctr_1_opctr));
  ALUCtr aluctr_1 (.Cin(ALUctr), .SUBctr(aluctr_1_subctr), .SIGctr(aluctr_1_sigctr), .OPctr(aluctr_1_opctr));
  Multiplexer #(.enable("false")) multiplexer_2 (
    .in0(xor_2_out), .in1(xor_3_out), .out(multiplexer_2_out), .sel(aluctr_1_sigctr));
  assign bit_extender_2_out = {{31{1'b0}}, multiplexer_2_out};  // Bit_Extender bit_extender_2
endmodule

module \指令分解  (
  input  [31:0] \输入指令 ,
  input  [2:0] Extop,
  output [6:0] op,
  output [4:0] rd,
  output [2:0] funct3,
  output [4:0] rs1,
  output [4:0] rs2,
  output [6:0] funct7,
  output [31:0] imm
);

  InstrToimm instrtoimm_1 (.INSTRUCTION(\输入指令 ), .Imm(imm), .EXTOP(Extop));

  assign funct3 = \输入指令 [14:12];
  assign funct7 = \输入指令 [31:25];
  assign op = \输入指令 [6:0];
  assign rd = \输入指令 [11:7];
  assign rs1 = \输入指令 [19:15];
  assign rs2 = \输入指令 [24:20];
endmodule

module InstrToimm (
  input  [31:0] INSTRUCTION,
  input  [2:0] EXTOP,
  output [31:0] Imm
);

  wire [11:0] bit_extender_4_out;
  wire [19:0] bit_extender_1_out, bit_extender_2_out, bit_extender_3_out;

  assign bit_extender_1_out = {{19{INSTRUCTION[31]}}, INSTRUCTION[31]};  // Bit_Extender bit_extender_1
  assign bit_extender_2_out = {{19{INSTRUCTION[31]}}, INSTRUCTION[31]};  // Bit_Extender bit_extender_2
  assign bit_extender_3_out = {{19{INSTRUCTION[31]}}, INSTRUCTION[31]};  // Bit_Extender bit_extender_3
  assign bit_extender_4_out = {{11{INSTRUCTION[31]}}, INSTRUCTION[31]};  // Bit_Extender bit_extender_4
  Multiplexer #(.select(3), .width(32), .enable("false")) multiplexer_1 (
    .in0({bit_extender_1_out, INSTRUCTION[31:20]}), .in1({INSTRUCTION[31:12], {12{1'b0}}}),
    .in2({bit_extender_2_out, INSTRUCTION[31:25], INSTRUCTION[11:7]}),
    .in3({bit_extender_3_out, INSTRUCTION[7], INSTRUCTION[30:25], INSTRUCTION[11:8], 1'b0}),
    .in4({bit_extender_4_out, INSTRUCTION[19:12], INSTRUCTION[20], INSTRUCTION[30:21], 1'b0}),
    .in5({32{1'b0}}), .in6({32{1'b0}}), .in7({32{1'b0}}), .out(Imm), .sel(EXTOP));

  // Notes on the sheet:
  //   I
  //   U
  //   S
  //   B
  //   J
endmodule

module \取指令部件  (
  input  in_1,
  input  [31:0] imm,
  input  [2:0] extop,
  input  JUMP,
  input  BRANCH,
  input  ZERO,
  output [6:0] op,
  output [4:0] rd,
  output [2:0] funct3,
  output [4:0] rs1,
  output [4:0] rs2,
  output [6:0] funct7,
  output [31:0] imm_2
);

  wire CLK_out, RESET_out;
  wire [31:0] Pc_q, rom_1_data, \下地址逻辑_1_to_pc ;

  Register #(.width(32), .Select("low")) Pc (
    .D(\下地址逻辑_1_to_pc ), .Q(Pc_q), .clk(CLK_out), .clr(RESET_out));  // open: en
  Clock CLK (.out(CLK_out));
  Button RESET (.out(RESET_out));
  \下地址逻辑  \u_下地址逻辑_1  (.PCin(Pc_q), .imm(imm), .JUMP(JUMP), .TO_PC(\下地址逻辑_1_to_pc ), .BRANCH(BRANCH), .ZERO(ZERO));
  ROM #(.addrWidth(12), .dataWidth(32), .Select("low")) rom_1 (.addr(Pc_q[13:2]), .data(rom_1_data), .sel(in_1));
  \指令分解  \u_指令分解_1  (
    .\输入指令 (rom_1_data), .Extop(extop), .op(op), .rd(rd), .funct3(funct3), .rs1(rs1), .rs2(rs2),
    .funct7(funct7), .imm(imm_2));

  // Notes on the sheet:
  //               指令分解
  //   contents of rom_1 (hex, n*v repeats v):
  //   256*0 12b7 fff28293 5de1863 288000ef 112623
endmodule

module \下地址逻辑  (
  input  [31:0] PCin,
  input  [31:0] imm,
  input  JUMP,
  input  BRANCH,
  input  ZERO,
  output [31:0] TO_PC
);

  wire and_1_out, or_1_out;
  wire [31:0] multiplexer_1_out;

  Multiplexer #(.width(32), .enable("false")) multiplexer_1 (
    .in0(32'h4), .in1(imm), .out(multiplexer_1_out), .sel(or_1_out));
  or or_1 (or_1_out, JUMP, and_1_out);
  and and_1 (and_1_out, BRANCH, ZERO);
  \_32位加法器  \u_32位加法器_1  (.C0(1'b0), .A(PCin), .B(multiplexer_1_out), .out_6(TO_PC));  // open: ZF, CF, OF, SF
endmodule
