// Logisim project LAB 5-3.circ as structural Verilog: 1 circuit, main circuit main
module main (
  input  [6:0] OP_6_0,
  input  [2:0] fn_2_0,
  output REGwr,
  output MEMTOREG,
  output MEMWR,
  output BRANCH,
  output JUMP,
  output [3:0] ALUctr_3_0,
  output ALUASrc,
  output [1:0] ALUBSrc,
  output [2:0] EXTOP
);

  wire and_1_out, and_2_out, and_3_out, and_4_out, and_5_out, and_6_out, and_7_out, \I型_out , Lui_out,
       not_1_out, not_2_out, not_3_out, or_1_out, or_2_out, \R型_out ;

  and \R型  (\R型_out , ~OP_6_0[6], OP_6_0[5], OP_6_0[4], ~OP_6_0[3], ~OP_6_0[2], OP_6_0[1], OP_6_0[0]);  // AND_Gate
  and \I型  (\I型_out , ~OP_6_0[6], ~OP_6_0[5], OP_6_0[4], ~OP_6_0[3], ~OP_6_0[2], OP_6_0[1], OP_6_0[0]);  // AND_Gate
  or or_1 (or_1_out, \R型_out , \I型_out );
  and and_1 (and_1_out, or_1_out, fn_2_0[2]);
  and and_2 (and_2_out, or_1_out, fn_2_0[1]);
  and and_3 (and_3_out, or_1_out, fn_2_0[0]);
  and Lui (Lui_out, ~OP_6_0[6], OP_6_0[5], OP_6_0[4], ~OP_6_0[3], OP_6_0[2], OP_6_0[1], OP_6_0[0]);  // AND_Gate
  and Load (MEMTOREG, ~OP_6_0[6], ~OP_6_0[5], ~OP_6_0[4], ~OP_6_0[3], ~OP_6_0[2], OP_6_0[1], OP_6_0[0]);  // AND_Gate
  and and_4 (and_4_out, \I型_out , fn_2_0[1], fn_2_0[2]);
  and Store (MEMWR, ~OP_6_0[6], OP_6_0[5], ~OP_6_0[4], ~OP_6_0[3], ~OP_6_0[2], OP_6_0[1], OP_6_0[0]);  // AND_Gate
  or or_2 (or_2_out, MEMTOREG, MEMWR);
  and \B型  (BRANCH, OP_6_0[6], OP_6_0[5], ~OP_6_0[4], ~OP_6_0[3], ~OP_6_0[2], OP_6_0[1], OP_6_0[0]);  // AND_Gate
  not not_1 (not_1_out, fn_2_0[0]);
  not not_2 (not_2_out, fn_2_0[1]);
  not not_3 (not_3_out, fn_2_0[2]);
  and \J型  (ALUASrc, OP_6_0[6], OP_6_0[5], ~OP_6_0[4], OP_6_0[3], OP_6_0[2], OP_6_0[1], OP_6_0[0]);  // AND_Gate
  and and_5 (and_5_out, or_2_out, fn_2_0[1]);
  and and_6 (and_6_out, MEMWR, fn_2_0[1]);
  and and_7 (and_7_out, BRANCH, not_1_out, not_2_out, not_3_out);
  or or_3 (REGwr, \R型_out , \I型_out , Lui_out, MEMTOREG, ALUASrc);
  or or_4 (ALUctr_3_0[3], Lui_out, BRANCH);
  or or_5 (ALUctr_3_0[2], Lui_out, and_1_out);
  or or_6 (ALUctr_3_0[1], Lui_out, and_2_out);
  or or_7 (ALUctr_3_0[0], Lui_out, and_3_out);
  or or_8 (ALUBSrc[1], and_5_out, Lui_out, and_4_out);
  or or_9 (EXTOP[1], and_6_out, and_7_out);
  or or_10 (EXTOP[0], Lui_out, and_7_out);

  assign ALUBSrc[0] = ALUASrc;
  assign EXTOP[2] = ALUASrc;
  assign JUMP = ALUASrc;
endmodule
