// Logisim project 实验6.circ as structural Verilog: 19 circuits, main circuit 排序算法
module \排序算法  (
  input  ZERO,
  input  [31:0] in_2,
  output [31:0] Instr,
  output Branch,
  output [2:0] funct3,
  output Jump,
  output [6:0] OP,
  output RegWr,
  output ALUASrc,
  output [2:0] ExtOp,
  output [1:0] ALUBSrc,
  output [3:0] ALUctr,
  output MemWr,
  output MemtoReg
);

  wire alu_1_zero, and_1_out, Clock, not_1_out, or_1_out;
  wire [4:0] \指令解析_1_rd , \指令解析_1_rs1 , \指令解析_1_rs2 ;
  wire [31:0] adder_1_out, alu_1_result, multiplexer_1_out, multiplexer_2_out, multiplexer_3_out,
       multiplexer_4_out, n32_32_bit_registers_1_busa, n32_32_bit_registers_1_busb, PC_q, \数据存储器_data ,
       \立即数扩展器_1_imm ;

  Clock u_Clock (.out(Clock));
  ROM #(.addrWidth(12), .dataWidth(32), .Select("low")) \u_指令存储器  (.addr(PC_q[13:2]), .data(Instr));
  \指令解析  \u_指令解析_1  (
    .\输入指令 (Instr), .op(OP), .funct3(funct3), .Rs2(\指令解析_1_rs2 ), .Rs1(\指令解析_1_rs1 ), .Rd(\指令解析_1_rd ));  // open: ExtOp, funct7, imm
  \立即数扩展器  \u_立即数扩展器_1  (.Instr(Instr), .ExtOp(ExtOp), .imm(\立即数扩展器_1_imm ));
  _32_32_bit_Registers u_32_32_bit_registers_1 (
    .RW(\指令解析_1_rd ), .busW(multiplexer_4_out), .RB(\指令解析_1_rs2 ), .RA(\指令解析_1_rs1 ), .WE(RegWr),
    .in_6(Clock), .busA(n32_32_bit_registers_1_busa), .busB(n32_32_bit_registers_1_busb));
  Register #(.width(32), .trigger("falling"), .Select("low")) PC (
    .D(adder_1_out), .Q(PC_q), .clk(Clock));  // open: en, clr
  Multiplexer #(.width(32), .enable("false")) multiplexer_1 (
    .in0(n32_32_bit_registers_1_busa), .in1(PC_q), .out(multiplexer_1_out), .sel(ALUASrc));
  Adder #(.width(32)) adder_1 (.a(PC_q), .b(multiplexer_2_out), .out(adder_1_out));  // open: cin, cout
  Multiplexer #(.width(32), .enable("false")) multiplexer_2 (
    .in0(32'h4), .in1(\立即数扩展器_1_imm ), .out(multiplexer_2_out), .sel(or_1_out));
  ALU alu_1 (.A(multiplexer_1_out), .B(multiplexer_3_out), .ALUctr(ALUctr), .Zero(alu_1_zero), .Result(alu_1_result));
  Multiplexer #(.select(2), .width(32), .enable("false")) multiplexer_3 (
    .in0(n32_32_bit_registers_1_busb), .in1(32'h4), .in2(\立即数扩展器_1_imm ), .in3({32{1'b0}}),
    .out(multiplexer_3_out), .sel(ALUBSrc));
  or or_1 (or_1_out, and_1_out, Jump);
  and and_1 (and_1_out, alu_1_zero, Branch);
  not not_1 (not_1_out, MemWr);
  \RISC_V指令控制  \u_控制器  (
    .op(OP), .funct3(funct3), .Branch(Branch), .Jump(Jump), .MemtoReg(MemtoReg), .RegWr(RegWr),
    .ALUctr_3_0(ALUctr), .ALUBSrc_1_0(ALUBSrc), .ExtOp(ExtOp), .ALUASrc(ALUASrc), .MemWr(MemWr));
  RAM #(.addrWidth(12), .dataWidth(32), .bus("separate"), .Select("low")) \u_数据存储器  (
    .addr(alu_1_result[13:2]), .din(n32_32_bit_registers_1_busb), .data(\数据存储器_data ), .str(MemWr),
    .clk(Clock), .ld(not_1_out));  // open: sel, clr
  Multiplexer #(.width(32), .enable("false")) multiplexer_4 (
    .in0(alu_1_result), .in1(\数据存储器_data ), .out(multiplexer_4_out), .sel(MemtoReg));

  // Other names for the same wires on the sheet: Imm[31:0] = in_2

  // Notes on the sheet:
  //   contents of 指令存储器 (hex, n*v repeats v):
  //   2083 8133 106213 406293 fff06313 4410663 106193 406393 806413 21b5b3 2058063 3a483 42503 a4b5b3
  //   458c63 a3a023 942023 c0006f 610133 fc9ff06f 4181b3 5383b3 540433 fc9ff06f 6f
endmodule

// 扩展器
module \立即数扩展器  (
  input  [31:0] Instr,
  input  [2:0] ExtOp,
  output [31:0] imm
);

  wire [11:0] \n1_12符号扩展器_1_out_2 ;
  wire [19:0] \n1_20符号扩展器_1_out_2 , \n1_20符号扩展器_2_out_2 , \n1_20符号扩展器_3_out_2 ;

  \_1_20符号扩展器  \u_1_20符号扩展器_1  (.in_1(Instr[31]), .out_2(\n1_20符号扩展器_1_out_2 ));
  \_1_20符号扩展器  \u_1_20符号扩展器_2  (.in_1(Instr[31]), .out_2(\n1_20符号扩展器_2_out_2 ));
  \_1_20符号扩展器  \u_1_20符号扩展器_3  (.in_1(Instr[31]), .out_2(\n1_20符号扩展器_3_out_2 ));
  \_1_12符号扩展器  \u_1_12符号扩展器_1  (.in_1(Instr[31]), .out_2(\n1_12符号扩展器_1_out_2 ));
  Multiplexer #(.select(3), .width(32), .enable("false")) multiplexer_1 (
    .in0({\n1_20符号扩展器_1_out_2 , Instr[31:20]}), .in1({Instr[31:12], {12{1'b0}}}),
    .in2({\n1_20符号扩展器_2_out_2 , Instr[31:25], Instr[11:7]}),
    .in3({\n1_20符号扩展器_3_out_2 , Instr[7], Instr[30:25], Instr[11:8], 1'b0}),
    .in4({\n1_12符号扩展器_1_out_2 , Instr[19:12], Instr[20], Instr[30:21], 1'b0}), .in5({32{1'b0}}),
    .in6({32{1'b0}}), .in7({32{1'b0}}), .out(imm), .sel(ExtOp));
endmodule

module \_1_20符号扩展器  (
  input  in_1,
  output [19:0] out_2
);


  assign out_2 = {20{in_1}};
endmodule

module \_1_12符号扩展器  (
  input  in_1,
  output [11:0] out_2
);


  assign out_2 = {12{in_1}};
endmodule

// 寄存器堆
module _32_32_bit_Registers (
  input  [4:0] RW,
  input  [31:0] busW,
  input  [4:0] RB,
  input  [4:0] RA,
  input  WE,
  input  in_6,
  output [31:0] busA,
  output [31:0] busB
);

  wire and_1_out, and_2_out, and_3_out, and_4_out, and_5_out, and_6_out, and_7_out, and_8_out, and_9_out,
       and_10_out, and_11_out, and_12_out, and_13_out, and_14_out, and_15_out, and_16_out, and_17_out,
       and_18_out, and_19_out, and_20_out, and_21_out, and_22_out, and_23_out, and_24_out, and_25_out,
       and_26_out, and_27_out, and_28_out, and_29_out, and_30_out, and_31_out, and_32_out, decoder_1_out0,
       decoder_1_out1, decoder_1_out2, decoder_1_out3, decoder_1_out4, decoder_1_out5, decoder_1_out6,
       decoder_1_out7, decoder_1_out8, decoder_1_out9, decoder_1_out10, decoder_1_out11, decoder_1_out12,
       decoder_1_out13, decoder_1_out14, decoder_1_out15, decoder_1_out16, decoder_1_out17, decoder_1_out18,
       decoder_1_out19, decoder_1_out20, decoder_1_out21, decoder_1_out22, decoder_1_out23, decoder_1_out24,
       decoder_1_out25, decoder_1_out26, decoder_1_out27, decoder_1_out28, decoder_1_out29, decoder_1_out30,
       decoder_1_out31;
  wire [31:0] \寄存器0_q , \寄存器1_q , \寄存器2_q , \寄存器3_q , \寄存器4_q , \寄存器5_q , \寄存器6_q , \寄存器7_q , \寄存器8_q ,
       \寄存器9_q , \寄存器10_q , \寄存器11_q , \寄存器12_q , \寄存器13_q , \寄存器14_q , \寄存器15_q , \寄存器16_q , \寄存器17_q ,
       \寄存器18_q , \寄存器19_q , \寄存器20_q , \寄存器21_q , \寄存器22_q , \寄存器23_q , \寄存器24_q , \寄存器25_q , \寄存器26_q ,
       \寄存器27_q , \寄存器28_q , \寄存器29_q , \寄存器30_q , \寄存器31_q ;

  Decoder #(.select(5), .enable("false")) decoder_1 (
    .out0(decoder_1_out0), .out1(decoder_1_out1), .out2(decoder_1_out2), .out3(decoder_1_out3),
    .out4(decoder_1_out4), .out5(decoder_1_out5), .out6(decoder_1_out6), .out7(decoder_1_out7),
    .out8(decoder_1_out8), .out9(decoder_1_out9), .out10(decoder_1_out10), .out11(decoder_1_out11),
    .out12(decoder_1_out12), .out13(decoder_1_out13), .out14(decoder_1_out14), .out15(decoder_1_out15),
    .out16(decoder_1_out16), .out17(decoder_1_out17), .out18(decoder_1_out18), .out19(decoder_1_out19),
    .out20(decoder_1_out20), .out21(decoder_1_out21), .out22(decoder_1_out22), .out23(decoder_1_out23),
    .out24(decoder_1_out24), .out25(decoder_1_out25), .out26(decoder_1_out26), .out27(decoder_1_out27),
    .out28(decoder_1_out28), .out29(decoder_1_out29), .out30(decoder_1_out30), .out31(decoder_1_out31),
    .sel(RW));
  and and_1 (and_1_out, WE, in_6, decoder_1_out0);
  and and_2 (and_2_out, WE, in_6, decoder_1_out1);
  and and_3 (and_3_out, WE, in_6, decoder_1_out2);
  and and_4 (and_4_out, WE, in_6, decoder_1_out3);
  and and_5 (and_5_out, WE, in_6, decoder_1_out4);
  and and_6 (and_6_out, WE, in_6, decoder_1_out5);
  and and_7 (and_7_out, WE, in_6, decoder_1_out6);
  and and_8 (and_8_out, WE, in_6, decoder_1_out7);
  and and_9 (and_9_out, decoder_1_out8, in_6, WE);
  and and_10 (and_10_out, decoder_1_out9, in_6, WE);
  and and_11 (and_11_out, decoder_1_out10, in_6, WE);
  and and_12 (and_12_out, decoder_1_out11, in_6, WE);
  and and_13 (and_13_out, decoder_1_out12, in_6, WE);
  and and_14 (and_14_out, decoder_1_out13, in_6, WE);
  and and_15 (and_15_out, decoder_1_out14, in_6, WE);
  and and_16 (and_16_out, in_6, decoder_1_out15, WE);
  and and_17 (and_17_out, decoder_1_out16, in_6, WE);
  and and_18 (and_18_out, decoder_1_out17, in_6, WE);
  and and_19 (and_19_out, decoder_1_out18, in_6, WE);
  and and_20 (and_20_out, decoder_1_out19, in_6, WE);
  and and_21 (and_21_out, decoder_1_out20, in_6, WE);
  and and_22 (and_22_out, decoder_1_out21, in_6, WE);
  and and_23 (and_23_out, decoder_1_out22, in_6, WE);
  and and_24 (and_24_out, decoder_1_out23, in_6, WE);
  and and_25 (and_25_out, decoder_1_out24, in_6, WE);
  and and_26 (and_26_out, decoder_1_out25, in_6, WE);
  and and_27 (and_27_out, decoder_1_out26, in_6, WE);
  and and_28 (and_28_out, decoder_1_out27, in_6, WE);
  and and_29 (and_29_out, decoder_1_out28, in_6, WE);
  and and_30 (and_30_out, decoder_1_out29, in_6, WE);
  and and_31 (and_31_out, decoder_1_out30, in_6, WE);
  and and_32 (and_32_out, decoder_1_out31, in_6, WE);
  Register #(.width(32), .Select("low")) \u_寄存器0  (.D(busW), .en(1'b0), .Q(\寄存器0_q ), .clk(and_1_out));  // open: clr
  Register #(.width(32), .Select("low")) \u_寄存器1  (.D(busW), .Q(\寄存器1_q ), .clk(and_2_out));  // open: en, clr
  Register #(.width(32), .Select("low")) \u_寄存器2  (.D(busW), .Q(\寄存器2_q ), .clk(and_3_out));  // open: en, clr
  Register #(.width(32), .Select("low")) \u_寄存器3  (.D(busW), .Q(\寄存器3_q ), .clk(and_4_out));  // open: en, clr
  Register #(.width(32), .Select("low")) \u_寄存器4  (.D(busW), .Q(\寄存器4_q ), .clk(and_5_out));  // open: en, clr
  Register #(.width(32), .Select("low")) \u_寄存器5  (.D(busW), .Q(\寄存器5_q ), .clk(and_6_out));  // open: en, clr
  Register #(.width(32), .Select("low")) \u_寄存器6  (.D(busW), .Q(\寄存器6_q ), .clk(and_7_out));  // open: en, clr
  Register #(.width(32), .Select("low")) \u_寄存器7  (.D(busW), .Q(\寄存器7_q ), .clk(and_8_out));  // open: en, clr
  Register #(.width(32), .Select("low")) \u_寄存器8  (.D(busW), .Q(\寄存器8_q ), .clk(and_9_out));  // open: en, clr
  Register #(.width(32), .Select("low")) \u_寄存器9  (.D(busW), .Q(\寄存器9_q ), .clk(and_10_out));  // open: en, clr
  Register #(.width(32), .Select("low")) \u_寄存器10  (.D(busW), .Q(\寄存器10_q ), .clk(and_11_out));  // open: en, clr
  Register #(.width(32), .Select("low")) \u_寄存器11  (.D(busW), .Q(\寄存器11_q ), .clk(and_12_out));  // open: en, clr
  Register #(.width(32), .Select("low")) \u_寄存器12  (.D(busW), .Q(\寄存器12_q ), .clk(and_13_out));  // open: en, clr
  Register #(.width(32), .Select("low")) \u_寄存器13  (.D(busW), .Q(\寄存器13_q ), .clk(and_14_out));  // open: en, clr
  Register #(.width(32), .Select("low")) \u_寄存器14  (.D(busW), .Q(\寄存器14_q ), .clk(and_15_out));  // open: en, clr
  Register #(.width(32), .Select("low")) \u_寄存器15  (.D(busW), .Q(\寄存器15_q ), .clk(and_16_out));  // open: en, clr
  Register #(.width(32), .Select("low")) \u_寄存器16  (.D(busW), .Q(\寄存器16_q ), .clk(and_17_out));  // open: en, clr
  Register #(.width(32), .Select("low")) \u_寄存器17  (.D(busW), .Q(\寄存器17_q ), .clk(and_18_out));  // open: en, clr
  Register #(.width(32), .Select("low")) \u_寄存器18  (.D(busW), .Q(\寄存器18_q ), .clk(and_19_out));  // open: en, clr
  Register #(.width(32), .Select("low")) \u_寄存器19  (.D(busW), .Q(\寄存器19_q ), .clk(and_20_out));  // open: en, clr
  Register #(.width(32), .Select("low")) \u_寄存器20  (.D(busW), .Q(\寄存器20_q ), .clk(and_21_out));  // open: en, clr
  Register #(.width(32), .Select("low")) \u_寄存器21  (.D(busW), .Q(\寄存器21_q ), .clk(and_22_out));  // open: en, clr
  Register #(.width(32), .Select("low")) \u_寄存器22  (.D(busW), .Q(\寄存器22_q ), .clk(and_23_out));  // open: en, clr
  Register #(.width(32), .Select("low")) \u_寄存器23  (.D(busW), .Q(\寄存器23_q ), .clk(and_24_out));  // open: en, clr
  Register #(.width(32), .Select("low")) \u_寄存器24  (.D(busW), .Q(\寄存器24_q ), .clk(and_25_out));  // open: en, clr
  Register #(.width(32), .Select("low")) \u_寄存器25  (.D(busW), .Q(\寄存器25_q ), .clk(and_26_out));  // open: en, clr
  Register #(.width(32), .Select("low")) \u_寄存器26  (.D(busW), .Q(\寄存器26_q ), .clk(and_27_out));  // open: en, clr
  Register #(.width(32), .Select("low")) \u_寄存器27  (.D(busW), .Q(\寄存器27_q ), .clk(and_28_out));  // open: en, clr
  Register #(.width(32), .Select("low")) \u_寄存器28  (.D(busW), .Q(\寄存器28_q ), .clk(and_29_out));  // open: en, clr
  Register #(.width(32), .Select("low")) \u_寄存器29  (.D(busW), .Q(\寄存器29_q ), .clk(and_30_out));  // open: en, clr
  Register #(.width(32), .Select("low")) \u_寄存器30  (.D(busW), .Q(\寄存器30_q ), .clk(and_31_out));  // open: en, clr
  Register #(.width(32), .Select("low")) \u_寄存器31  (.D(busW), .Q(\寄存器31_q ), .clk(and_32_out));  // open: en, clr
  Multiplexer #(.select(5), .width(32), .enable("false")) multiplexer_1 (
    .in0(\寄存器0_q ), .in1(\寄存器1_q ), .in2(\寄存器2_q ), .in3(\寄存器3_q ), .in4(\寄存器4_q ), .in5(\寄存器5_q ),
    .in6(\寄存器6_q ), .in7(\寄存器7_q ), .in8(\寄存器8_q ), .in9(\寄存器9_q ), .in10(\寄存器10_q ), .in11(\寄存器11_q ),
    .in12(\寄存器12_q ), .in13(\寄存器13_q ), .in14(\寄存器14_q ), .in15(\寄存器15_q ), .in16(\寄存器16_q ),
    .in17(\寄存器17_q ), .in18(\寄存器18_q ), .in19(\寄存器19_q ), .in20(\寄存器20_q ), .in21(\寄存器21_q ),
    .in22(\寄存器22_q ), .in23(\寄存器23_q ), .in24(\寄存器24_q ), .in25(\寄存器25_q ), .in26(\寄存器26_q ),
    .in27(\寄存器27_q ), .in28(\寄存器28_q ), .in29(\寄存器29_q ), .in30(\寄存器30_q ), .in31(\寄存器31_q ), .out(busA),
    .sel(RA));
  Multiplexer #(.select(5), .width(32), .enable("false")) multiplexer_2 (
    .in0(\寄存器0_q ), .in1(\寄存器1_q ), .in2(\寄存器2_q ), .in3(\寄存器3_q ), .in4(\寄存器4_q ), .in5(\寄存器5_q ),
    .in6(\寄存器6_q ), .in7(\寄存器7_q ), .in8(\寄存器8_q ), .in9(\寄存器9_q ), .in10(\寄存器10_q ), .in11(\寄存器11_q ),
    .in12(\寄存器12_q ), .in13(\寄存器13_q ), .in14(\寄存器14_q ), .in15(\寄存器15_q ), .in16(\寄存器16_q ),
    .in17(\寄存器17_q ), .in18(\寄存器18_q ), .in19(\寄存器19_q ), .in20(\寄存器20_q ), .in21(\寄存器21_q ),
    .in22(\寄存器22_q ), .in23(\寄存器23_q ), .in24(\寄存器24_q ), .in25(\寄存器25_q ), .in26(\寄存器26_q ),
    .in27(\寄存器27_q ), .in28(\寄存器28_q ), .in29(\寄存器29_q ), .in30(\寄存器30_q ), .in31(\寄存器31_q ), .out(busB),
    .sel(RB));
endmodule

module \符号扩展  (
  input  in_1,
  output [31:0] out_2
);


  assign out_2 = {32{in_1}};
endmodule

module \_0扩展  (
  input  in_1,
  output [31:0] out_2
);


  assign out_2 = {{31{1'b0}}, in_1};
endmodule

module \异或门阵列  (
  input  [31:0] in_1,
  input  [31:0] in_2,
  output [31:0] out_3
);

  xor xor_1 (out_3[0], in_1[0], in_2[0]);
  xor xor_2 (out_3[1], in_1[1], in_2[1]);
  xor xor_3 (out_3[2], in_1[2], in_2[2]);
  xor xor_4 (out_3[3], in_1[3], in_2[3]);
  xor xor_5 (out_3[4], in_1[4], in_2[4]);
  xor xor_6 (out_3[5], in_1[5], in_2[5]);
  xor xor_7 (out_3[6], in_1[6], in_2[6]);
  xor xor_8 (out_3[7], in_1[7], in_2[7]);
  xor xor_9 (out_3[8], in_1[8], in_2[8]);
  xor xor_10 (out_3[9], in_1[9], in_2[9]);
  xor xor_11 (out_3[10], in_1[10], in_2[10]);
  xor xor_12 (out_3[11], in_1[11], in_2[11]);
  xor xor_13 (out_3[12], in_1[12], in_2[12]);
  xor xor_14 (out_3[13], in_1[13], in_2[13]);
  xor xor_15 (out_3[14], in_1[14], in_2[14]);
  xor xor_16 (out_3[15], in_1[15], in_2[15]);
  xor xor_17 (out_3[16], in_1[16], in_2[16]);
  xor xor_18 (out_3[17], in_1[17], in_2[17]);
  xor xor_19 (out_3[18], in_1[18], in_2[18]);
  xor xor_20 (out_3[19], in_1[19], in_2[19]);
  xor xor_21 (out_3[20], in_1[20], in_2[20]);
  xor xor_22 (out_3[21], in_1[21], in_2[21]);
  xor xor_23 (out_3[22], in_1[22], in_2[22]);
  xor xor_24 (out_3[23], in_1[23], in_2[23]);
  xor xor_25 (out_3[24], in_1[24], in_2[24]);
  xor xor_26 (out_3[25], in_1[25], in_2[25]);
  xor xor_27 (out_3[26], in_1[26], in_2[26]);
  xor xor_28 (out_3[27], in_1[27], in_2[27]);
  xor xor_29 (out_3[28], in_1[28], in_2[28]);
  xor xor_30 (out_3[29], in_1[29], in_2[29]);
  xor xor_31 (out_3[30], in_1[30], in_2[30]);
  xor xor_32 (out_3[31], in_1[31], in_2[31]);
endmodule

module \或门阵列  (
  input  [31:0] in_1,
  input  [31:0] in_2,
  output [31:0] out_3
);

  or or_1 (out_3[0], in_1[0], in_2[0]);
  or or_2 (out_3[1], in_1[1], in_2[1]);
  or or_3 (out_3[2], in_1[2], in_2[2]);
  or or_4 (out_3[3], in_1[3], in_2[3]);
  or or_5 (out_3[4], in_1[4], in_2[4]);
  or or_6 (out_3[5], in_1[5], in_2[5]);
  or or_7 (out_3[6], in_1[6], in_2[6]);
  or or_8 (out_3[7], in_1[7], in_2[7]);
  or or_9 (out_3[8], in_1[8], in_2[8]);
  or or_10 (out_3[9], in_1[9], in_2[9]);
  or or_11 (out_3[10], in_1[10], in_2[10]);
  or or_12 (out_3[11], in_1[11], in_2[11]);
  or or_13 (out_3[12], in_1[12], in_2[12]);
  or or_14 (out_3[13], in_1[13], in_2[13]);
  or or_15 (out_3[14], in_1[14], in_2[14]);
  or or_16 (out_3[15], in_1[15], in_2[15]);
  or or_17 (out_3[16], in_1[16], in_2[16]);
  or or_18 (out_3[17], in_1[17], in_2[17]);
  or or_19 (out_3[18], in_1[18], in_2[18]);
  or or_20 (out_3[19], in_1[19], in_2[19]);
  or or_21 (out_3[20], in_1[20], in_2[20]);
  or or_22 (out_3[21], in_1[21], in_2[21]);
  or or_23 (out_3[22], in_1[22], in_2[22]);
  or or_24 (out_3[23], in_1[23], in_2[23]);
  or or_25 (out_3[24], in_1[24], in_2[24]);
  or or_26 (out_3[25], in_1[25], in_2[25]);
  or or_27 (out_3[26], in_1[26], in_2[26]);
  or or_28 (out_3[27], in_1[27], in_2[27]);
  or or_29 (out_3[28], in_1[28], in_2[28]);
  or or_30 (out_3[29], in_1[29], in_2[29]);
  or or_31 (out_3[30], in_1[30], in_2[30]);
  or or_32 (out_3[31], in_1[31], in_2[31]);
endmodule

module CLA (
  input  B3,
  input  A3,
  input  B2,
  input  A2,
  input  B1,
  input  A1,
  input  B0,
  input  A0,
  input  C0,
  output C4,
  output S3,
  output S2,
  output S1,
  output S0
);

  wire and_1_out, and_2_out, and_3_out, and_4_out, and_6_out, and_7_out, and_8_out, nand_1_out, nand_2_out,
       nand_3_out, nand_4_out, nor_1_out, nor_2_out, nor_3_out, nor_4_out, not_1_out, not_2_out, not_3_out,
       not_4_out, not_5_out, not_6_out, not_7_out, not_8_out, not_9_out, not_10_out, not_11_out, not_12_out,
       not_13_out, not_14_out, not_15_out, not_16_out, not_17_out, not_18_out, not_19_out, not_20_out,
       not_21_out, not_22_out, not_23_out, not_24_out, not_25_out, not_26_out, not_27_out, not_28_out,
       not_29_out, not_30_out, not_31_out, not_32_out, not_33_out, not_34_out, not_35_out, not_36_out,
       not_37_out, not_38_out, not_39_out, not_40_out, or_1_out, or_2_out, or_3_out, or_4_out, or_5_out,
       or_6_out, or_7_out, or_8_out, or_9_out, or_10_out;

  nand nand_1 (nand_1_out, B3, A3);
  nor nor_1 (nor_1_out, B3, A3);
  nand nand_2 (nand_2_out, B2, A2);
  nor nor_2 (nor_2_out, B2, A2);
  nand nand_3 (nand_3_out, B1, A1);
  nor nor_3 (nor_3_out, B1, A1);
  nand nand_4 (nand_4_out, B0, A0);
  nor nor_4 (nor_4_out, B0, A0);
  not not_1 (not_1_out, C0);
  not not_2 (not_2_out, nor_1_out);
  not not_3 (not_3_out, nor_2_out);
  not not_4 (not_4_out, nand_1_out);
  not not_5 (not_5_out, nor_3_out);
  not not_6 (not_6_out, nand_1_out);
  not not_7 (not_7_out, nand_2_out);
  not not_8 (not_8_out, nor_4_out);
  not not_9 (not_9_out, nand_1_out);
  not not_10 (not_10_out, nand_2_out);
  not not_11 (not_11_out, nand_3_out);
  not not_12 (not_12_out, nand_1_out);
  not not_13 (not_13_out, nand_2_out);
  not not_14 (not_14_out, nand_3_out);
  not not_15 (not_15_out, nand_4_out);
  not not_16 (not_16_out, not_1_out);
  not not_17 (not_17_out, nor_1_out);
  not not_18 (not_18_out, nor_2_out);
  not not_19 (not_19_out, nor_3_out);
  not not_20 (not_20_out, nand_2_out);
  not not_21 (not_21_out, nor_4_out);
  not not_22 (not_22_out, nand_2_out);
  not not_23 (not_23_out, nand_3_out);
  not not_24 (not_24_out, nand_2_out);
  not not_25 (not_25_out, nand_3_out);
  not not_26 (not_26_out, nand_4_out);
  not not_27 (not_27_out, not_1_out);
  not not_28 (not_28_out, nor_2_out);
  not not_29 (not_29_out, nor_3_out);
  not not_30 (not_30_out, nor_4_out);
  not not_31 (not_31_out, nand_3_out);
  not not_32 (not_32_out, nand_3_out);
  not not_33 (not_33_out, nand_4_out);
  not not_34 (not_34_out, not_1_out);
  not not_35 (not_35_out, nor_3_out);
  not not_36 (not_36_out, nor_4_out);
  not not_37 (not_37_out, nand_4_out);
  not not_38 (not_38_out, not_1_out);
  not not_39 (not_39_out, nor_4_out);
  not not_40 (not_40_out, not_1_out);
  or or_1 (or_1_out, not_3_out, not_4_out);
  or or_2 (or_2_out, not_5_out, not_6_out, not_7_out);
  or or_3 (or_3_out, not_8_out, not_9_out, not_10_out, not_11_out);
  or or_4 (or_4_out, not_12_out, not_13_out, not_14_out, not_15_out, not_16_out);
  and and_1 (and_1_out, nand_1_out, not_17_out);
  or or_5 (or_5_out, not_19_out, not_20_out);
  or or_6 (or_6_out, not_21_out, not_22_out, not_23_out);
  or or_7 (or_7_out, not_24_out, not_25_out, not_26_out, not_27_out);
  and and_2 (and_2_out, nand_2_out, not_28_out);
  or or_8 (or_8_out, not_30_out, not_31_out);
  or or_9 (or_9_out, not_32_out, not_33_out, not_34_out);
  and and_3 (and_3_out, nand_3_out, not_35_out);
  or or_10 (or_10_out, not_37_out, not_38_out);
  and and_4 (and_4_out, nand_4_out, not_39_out);
  and and_5 (C4, not_2_out, or_1_out, or_2_out, or_3_out, or_4_out);
  and and_6 (and_6_out, not_18_out, or_5_out, or_6_out, or_7_out);
  and and_7 (and_7_out, not_29_out, or_8_out, or_9_out);
  and and_8 (and_8_out, not_36_out, or_10_out);
  xor xor_1 (S3, and_1_out, and_6_out);
  xor xor_2 (S2, and_2_out, and_7_out);
  xor xor_3 (S1, and_3_out, and_8_out);
  xor xor_4 (S0, and_4_out, not_40_out);
endmodule

module CLU (
  input  X3,
  input  Y3,
  input  X2,
  input  Y2,
  input  X1,
  input  Y1,
  input  X0,
  input  Y0,
  input  C0,
  output C4,
  output C3,
  output C2,
  output C1
);

  wire and_1_out, and_2_out, and_3_out, and_4_out, and_5_out, and_6_out, and_7_out, and_8_out, and_9_out,
       and_10_out, G0_out, G1_out, G2_out, G3_out, P0_out, P1_out, P2_out, P3_out;

  and G3 (G3_out, X3, Y3);
  or P3 (P3_out, X3, Y3);
  and G2 (G2_out, X2, Y2);
  or P2 (P2_out, X2, Y2);
  and G1 (G1_out, X1, Y1);
  or P1 (P1_out, X1, Y1);
  and G0 (G0_out, X0, Y0);
  or P0 (P0_out, X0, Y0);
  and and_1 (and_1_out, P3_out, P2_out, P1_out, P0_out, C0);
  and and_2 (and_2_out, P3_out, P2_out, P1_out, G0_out);
  and and_3 (and_3_out, G1_out, P2_out, P3_out);
  and and_4 (and_4_out, P3_out, G2_out);
  and and_5 (and_5_out, P2_out, P1_out, P0_out, C0);
  and and_6 (and_6_out, P2_out, P1_out, G0_out);
  and and_7 (and_7_out, P2_out, G1_out);
  and and_8 (and_8_out, P1_out, P0_out, C0);
  and and_9 (and_9_out, P1_out, G0_out);
  and and_10 (and_10_out, P0_out, C0);
  or or_1 (C4, and_1_out, and_2_out, G3_out, and_3_out, and_4_out);
  or or_2 (C3, and_5_out, G2_out, and_6_out, and_7_out);
  or or_3 (C2, G1_out, and_8_out, and_9_out);
  or or_4 (C1, G0_out, and_10_out);
endmodule

module _4_bit_adder (
  input  B3,
  input  A3,
  input  B2,
  input  A2,
  input  B1,
  input  A1,
  input  B0,
  input  A0,
  input  C0,
  output C4,
  output S3,
  output S2,
  output S1,
  output S0,
  output Gg,
  output Pg
);

  wire and_1_out, and_2_out, and_3_out, and_5_out, and_6_out, and_7_out, and_8_out, and_10_out, and_11_out,
       and_12_out, nand_1_out, nand_2_out, nand_3_out, nand_4_out, nor_1_out, nor_2_out, nor_3_out,
       nor_4_out, not_1_out, not_2_out, not_3_out, not_4_out, not_5_out, not_6_out, not_7_out, not_8_out,
       not_9_out, not_10_out, not_11_out, not_12_out, not_13_out, not_14_out, not_15_out, not_16_out,
       not_17_out, not_18_out, not_19_out, not_20_out, not_21_out, not_22_out, not_23_out, not_24_out,
       not_25_out, not_26_out, not_27_out, not_28_out, not_29_out, not_30_out, not_31_out, not_32_out,
       not_33_out, not_34_out, not_35_out, not_36_out, not_37_out, not_38_out, not_39_out, not_40_out,
       not_41_out, not_42_out, not_43_out, not_44_out, not_45_out, not_46_out, not_47_out, not_48_out,
       not_49_out, not_50_out, not_51_out, not_52_out, not_53_out, not_54_out, or_2_out, or_3_out, or_4_out,
       or_5_out, or_6_out, or_7_out, or_8_out, or_9_out, or_10_out, or_11_out;

  nand nand_1 (nand_1_out, B3, A3);
  nor nor_1 (nor_1_out, B3, A3);
  nand nand_2 (nand_2_out, B2, A2);
  nor nor_2 (nor_2_out, B2, A2);
  nand nand_3 (nand_3_out, B1, A1);
  nor nor_3 (nor_3_out, B1, A1);
  nand nand_4 (nand_4_out, B0, A0);
  nor nor_4 (nor_4_out, B0, A0);
  not not_1 (not_1_out, C0);
  not not_2 (not_2_out, nor_1_out);
  not not_3 (not_3_out, nor_2_out);
  and and_1 (and_1_out, not_2_out, not_3_out, not_4_out, not_5_out);
  not not_4 (not_4_out, nor_3_out);
  not not_5 (not_5_out, nand_4_out);
  not not_6 (not_6_out, nor_1_out);
  not not_7 (not_7_out, nor_2_out);
  and and_2 (and_2_out, not_6_out, not_7_out, not_8_out);
  not not_8 (not_8_out, nand_3_out);
  not not_9 (not_9_out, nor_1_out);
  and and_3 (and_3_out, not_9_out, not_10_out);
  not not_10 (not_10_out, nand_2_out);
  not not_11 (not_11_out, nor_1_out);
  not not_12 (not_12_out, nor_2_out);
  and and_4 (Pg, not_11_out, not_12_out, not_13_out, not_14_out);
  not not_13 (not_13_out, nor_3_out);
  not not_14 (not_14_out, nor_4_out);
  not not_15 (not_15_out, nor_1_out);
  not not_16 (not_16_out, nor_2_out);
  not not_17 (not_17_out, nand_1_out);
  not not_18 (not_18_out, nor_3_out);
  not not_19 (not_19_out, nand_1_out);
  not not_20 (not_20_out, nand_2_out);
  not not_21 (not_21_out, nor_4_out);
  not not_22 (not_22_out, nand_1_out);
  not not_23 (not_23_out, nand_2_out);
  not not_24 (not_24_out, nand_3_out);
  not not_25 (not_25_out, nand_1_out);
  not not_26 (not_26_out, nand_2_out);
  not not_27 (not_27_out, nand_3_out);
  not not_28 (not_28_out, nand_4_out);
  not not_29 (not_29_out, not_1_out);
  not not_30 (not_30_out, nor_1_out);
  not not_31 (not_31_out, nor_2_out);
  not not_32 (not_32_out, nor_3_out);
  not not_33 (not_33_out, nand_2_out);
  not not_34 (not_34_out, nor_4_out);
  not not_35 (not_35_out, nand_2_out);
  not not_36 (not_36_out, nand_3_out);
  not not_37 (not_37_out, nand_2_out);
  not not_38 (not_38_out, nand_3_out);
  not not_39 (not_39_out, nand_4_out);
  not not_40 (not_40_out, not_1_out);
  not not_41 (not_41_out, nor_2_out);
  not not_42 (not_42_out, nor_3_out);
  not not_43 (not_43_out, nor_4_out);
  not not_44 (not_44_out, nand_3_out);
  not not_45 (not_45_out, nand_3_out);
  not not_46 (not_46_out, nand_4_out);
  not not_47 (not_47_out, not_1_out);
  not not_48 (not_48_out, nor_3_out);
  not not_49 (not_49_out, nor_4_out);
  not not_50 (not_50_out, nand_4_out);
  not not_51 (not_51_out, not_1_out);
  not not_52 (not_52_out, nor_4_out);
  not not_53 (not_53_out, not_1_out);
  or or_1 (Gg, and_1_out, and_2_out, and_3_out, not_54_out);
  not not_54 (not_54_out, nand_1_out);
  or or_2 (or_2_out, not_16_out, not_17_out);
  or or_3 (or_3_out, not_18_out, not_19_out, not_20_out);
  or or_4 (or_4_out, not_21_out, not_22_out, not_23_out, not_24_out);
  or or_5 (or_5_out, not_25_out, not_26_out, not_27_out, not_28_out, not_29_out);
  and and_5 (and_5_out, nand_1_out, not_30_out);
  or or_6 (or_6_out, not_32_out, not_33_out);
  or or_7 (or_7_out, not_34_out, not_35_out, not_36_out);
  or or_8 (or_8_out, not_37_out, not_38_out, not_39_out, not_40_out);
  and and_6 (and_6_out, nand_2_out, not_41_out);
  or or_9 (or_9_out, not_43_out, not_44_out);
  or or_10 (or_10_out, not_45_out, not_46_out, not_47_out);
  and and_7 (and_7_out, nand_3_out, not_48_out);
  or or_11 (or_11_out, not_50_out, not_51_out);
  and and_8 (and_8_out, nand_4_out, not_52_out);
  and and_9 (C4, not_15_out, or_2_out, or_3_out, or_4_out, or_5_out);
  and and_10 (and_10_out, not_31_out, or_6_out, or_7_out, or_8_out);
  and and_11 (and_11_out, not_42_out, or_9_out, or_10_out);
  and and_12 (and_12_out, not_49_out, or_11_out);
  xor xor_1 (S3, and_5_out, and_10_out);
  xor xor_2 (S2, and_6_out, and_11_out);
  xor xor_3 (S1, and_7_out, and_12_out);
  xor xor_4 (S0, and_8_out, not_53_out);
endmodule

module Gs_Ps (
  input  X3,
  input  Y3,
  input  X2,
  input  Y2,
  input  X1,
  input  Y1,
  input  X0,
  input  Y0,
  input  C0,
  output C4,
  output C3,
  output C2,
  output C1,
  output Ps,
  output Gs
);

  wire and_1_out, and_2_out, and_3_out, and_4_out, and_5_out, and_6_out, and_7_out, and_8_out, and_9_out,
       and_10_out, and_12_out, and_13_out, and_14_out, G0_out, G1_out, G2_out, G3_out, P0_out, P1_out,
       P2_out, P3_out;

  and G3 (G3_out, X3, Y3);
  or P3 (P3_out, X3, Y3);
  and G2 (G2_out, X2, Y2);
  or P2 (P2_out, X2, Y2);
  and G1 (G1_out, X1, Y1);
  or P1 (P1_out, X1, Y1);
  and G0 (G0_out, X0, Y0);
  or P0 (P0_out, X0, Y0);
  and and_1 (and_1_out, P3_out, P2_out, P1_out, P0_out, C0);
  and and_2 (and_2_out, P3_out, P2_out, P1_out, G0_out);
  and and_3 (and_3_out, G1_out, P2_out, P3_out);
  and and_4 (and_4_out, P3_out, G2_out);
  and and_5 (and_5_out, P2_out, P1_out, P0_out, C0);
  and and_6 (and_6_out, P2_out, P1_out, G0_out);
  and and_7 (and_7_out, P2_out, G1_out);
  and and_8 (and_8_out, P1_out, P0_out, C0);
  and and_9 (and_9_out, P1_out, G0_out);
  and and_10 (and_10_out, P0_out, C0);
  and and_11 (Ps, P3_out, P2_out, P1_out, P0_out);
  and and_12 (and_12_out, P3_out, P2_out, P1_out, G0_out);
  and and_13 (and_13_out, P3_out, P2_out, G1_out);
  and and_14 (and_14_out, P3_out, G2_out);
  or or_1 (C4, and_1_out, and_2_out, G3_out, and_3_out, and_4_out);
  or or_2 (C3, and_5_out, G2_out, and_6_out, and_7_out);
  or or_3 (C2, G1_out, and_8_out, and_9_out);
  or or_4 (C1, G0_out, and_10_out);
  or or_5 (Gs, and_12_out, and_13_out, and_14_out, G3_out);
endmodule

module \_16位先行进位加法器  (
  input  C0,
  input  [15:0] A,
  input  [15:0] B,
  output Ps,
  output Gs,
  output [15:0] S,
  output C16
);

  wire gs_ps_1_c1, gs_ps_1_c2, gs_ps_1_c3, n4_bit_adder_1_c4, n4_bit_adder_1_gg, n4_bit_adder_1_pg,
       n4_bit_adder_2_c4, n4_bit_adder_2_gg, n4_bit_adder_2_pg, n4_bit_adder_3_c4, n4_bit_adder_3_gg,
       n4_bit_adder_3_pg, n4_bit_adder_4_gg, n4_bit_adder_4_pg;

  _4_bit_adder u_4_bit_adder_1 (
    .B3(B[3]), .A3(A[3]), .B2(B[2]), .A2(A[2]), .B1(B[1]), .A1(A[1]), .B0(B[0]), .A0(A[0]), .C0(C0),
    .C4(n4_bit_adder_1_c4), .S3(S[3]), .S2(S[2]), .S1(S[1]), .S0(S[0]), .Gg(n4_bit_adder_1_gg),
    .Pg(n4_bit_adder_1_pg));
  _4_bit_adder u_4_bit_adder_2 (
    .B3(B[7]), .A3(A[7]), .B2(B[6]), .A2(A[6]), .B1(B[5]), .A1(A[5]), .B0(B[4]), .A0(A[4]),
    .C0(n4_bit_adder_1_c4), .C4(n4_bit_adder_2_c4), .S3(S[7]), .S2(S[6]), .S1(S[5]), .S0(S[4]),
    .Gg(n4_bit_adder_2_gg), .Pg(n4_bit_adder_2_pg));
  _4_bit_adder u_4_bit_adder_3 (
    .B3(B[11]), .A3(A[11]), .B2(B[10]), .A2(A[10]), .B1(B[9]), .A1(A[9]), .B0(B[8]), .A0(A[8]),
    .C0(n4_bit_adder_2_c4), .C4(n4_bit_adder_3_c4), .S3(S[11]), .S2(S[10]), .S1(S[9]), .S0(S[8]),
    .Gg(n4_bit_adder_3_gg), .Pg(n4_bit_adder_3_pg));
  _4_bit_adder u_4_bit_adder_4 (
    .B3(B[15]), .A3(A[15]), .B2(B[14]), .A2(A[14]), .B1(B[13]), .A1(A[13]), .B0(B[12]), .A0(A[12]),
    .C0(n4_bit_adder_3_c4), .C4(C16), .S3(S[15]), .S2(S[14]), .S1(S[13]), .S0(S[12]), .Gg(n4_bit_adder_4_gg),
    .Pg(n4_bit_adder_4_pg));
  Gs_Ps gs_ps_1 (
    .X3(n4_bit_adder_4_gg), .Y3(n4_bit_adder_4_pg), .X2(n4_bit_adder_3_gg), .Y2(n4_bit_adder_3_pg),
    .X1(n4_bit_adder_2_pg), .Y1(n4_bit_adder_2_gg), .X0(n4_bit_adder_1_pg), .Y0(n4_bit_adder_1_gg), .C0(C0),
    .C3(gs_ps_1_c3), .C2(gs_ps_1_c2), .C1(gs_ps_1_c1), .Ps(Ps), .Gs(Gs));  // open: C4
endmodule

module \_32位快速加法器  (
  input  Cin,
  input  [31:0] A,
  input  [31:0] B,
  output [31:0] F,
  output Cout,
  output CF,
  output ZF,
  output SF,
  output OF
);

  wire and_1_out, and_2_out, and_3_out, and_4_out, \n16位先行进位加法器_1_c16 , not_1_out, not_2_out, not_3_out,
       not_4_out, not_5_out, not_6_out, or_1_out;

  \_16位先行进位加法器  \u_16位先行进位加法器_1  (
    .C0(Cin), .A(A[15:0]), .B(B[15:0]), .S(F[15:0]), .C16(\n16位先行进位加法器_1_c16 ));  // open: Ps, Gs
  \_16位先行进位加法器  \u_16位先行进位加法器_2  (
    .C0(\n16位先行进位加法器_1_c16 ), .A(A[31:16]), .B(B[31:16]), .S(F[31:16]), .C16(Cout));  // open: Ps, Gs
  xor xor_1 (CF, Cout, Cin);
  not not_1 (not_1_out, A[31]);
  not not_2 (not_2_out, B[31]);
  not not_3 (not_3_out, F[31]);
  not not_4 (not_4_out, B[31]);
  not not_5 (not_5_out, F[31]);
  not not_6 (not_6_out, A[31]);
  nor nor_1 (ZF, F[0], F[1], F[2], F[3], F[4], F[5], F[6], F[7], F[8], F[9], F[10], F[11], F[12], F[13], F[14], F[15], F[16], F[17], F[18], F[19], F[20], F[21], F[22], F[23], F[24], F[25], F[26], F[27], F[28], F[29], F[30], F[31]);
  and and_1 (and_1_out, F[31], A[31], B[31]);
  and and_2 (and_2_out, F[31], not_1_out, not_2_out);
  and and_3 (and_3_out, not_3_out, not_4_out, A[31]);
  and and_4 (and_4_out, not_5_out, B[31], not_6_out);
  or or_1 (or_1_out, and_1_out, and_2_out, and_3_out, and_4_out);
  xor xor_2 (OF, Cout, or_1_out);

  assign SF = F[31];
endmodule

module \ALU操作控制信号生成部件  (
  input  [3:0] ALUctr_3_0,
  output [1:0] OPctr_1_0,
  output SUBctr,
  output SIGctr
);

  Multiplexer #(.select(4), .width(4), .enable("false")) multiplexer_1 (
    .in0(4'b0000), .in1(4'b0000), .in2(4'b1111), .in3(4'b1011), .in4(4'b0000), .in5(4'b0000), .in6(4'b0001),
    .in7(4'b0000), .in8(4'b1000), .in9(4'b0000), .in10(4'b0000), .in11(4'b0000), .in12(4'b0000),
    .in13(4'b0000), .in14(4'b0010), .in15(4'b1010), .out({SUBctr, SIGctr, OPctr_1_0}), .sel(ALUctr_3_0));
endmodule

module ALU (
  input  [31:0] A,
  input  [31:0] B,
  input  [3:0] ALUctr,
  output Zero,
  output [31:0] Result
);

  wire \alu操作控制信号生成部件_1_sigctr , \alu操作控制信号生成部件_1_subctr , multiplexer_2_out, \n32位快速加法器_1_cout ,
       \n32位快速加法器_1_of , \n32位快速加法器_1_sf , xor_1_out, xor_2_out;
  wire [1:0] \alu操作控制信号生成部件_1_opctr_1_0 ;
  wire [31:0] \n0扩展_1_out_2 , \n32位快速加法器_1_f , \异或门阵列_1_out_3 , \或门阵列_1_out_3 , \符号扩展_1_out_2 ;

  \符号扩展  \u_符号扩展_1  (.in_1(\alu操作控制信号生成部件_1_subctr ), .out_2(\符号扩展_1_out_2 ));
  \或门阵列  \u_或门阵列_1  (.in_1(A), .in_2(B), .out_3(\或门阵列_1_out_3 ));
  \异或门阵列  \u_异或门阵列_1  (.in_1(B), .in_2(\符号扩展_1_out_2 ), .out_3(\异或门阵列_1_out_3 ));
  \_32位快速加法器  \u_32位快速加法器_1  (
    .Cin(\alu操作控制信号生成部件_1_subctr ), .A(A), .B(\异或门阵列_1_out_3 ), .F(\n32位快速加法器_1_f ),
    .Cout(\n32位快速加法器_1_cout ), .ZF(Zero), .SF(\n32位快速加法器_1_sf ), .OF(\n32位快速加法器_1_of ));  // open: CF
  Multiplexer #(.select(2), .width(32), .enable("false")) multiplexer_1 (
    .in0(\n32位快速加法器_1_f ), .in1(\或门阵列_1_out_3 ), .in2(B), .in3(\n0扩展_1_out_2 ), .out(Result),
    .sel(\alu操作控制信号生成部件_1_opctr_1_0 ));
  \ALU操作控制信号生成部件  \alu操作控制信号生成部件_1  (
    .SUBctr(\alu操作控制信号生成部件_1_subctr ), .SIGctr(\alu操作控制信号生成部件_1_sigctr ),
    .OPctr_1_0(\alu操作控制信号生成部件_1_opctr_1_0 ), .ALUctr_3_0(ALUctr));
  xor xor_1 (xor_1_out, \alu操作控制信号生成部件_1_subctr , \n32位快速加法器_1_cout );
  xor xor_2 (xor_2_out, \n32位快速加法器_1_sf , \n32位快速加法器_1_of );
  Multiplexer #(.enable("false")) multiplexer_2 (
    .in0(xor_1_out), .in1(xor_2_out), .out(multiplexer_2_out), .sel(\alu操作控制信号生成部件_1_sigctr ));
  \_0扩展  \u_0扩展_1  (.in_1(multiplexer_2_out), .out_2(\n0扩展_1_out_2 ));
endmodule

module \RISC_V指令控制  (
  input  [6:0] op,
  input  [2:0] funct3,
  output Branch,
  output Jump,
  output MemtoReg,
  output RegWr,
  output [3:0] ALUctr_3_0,
  output [1:0] ALUBSrc_1_0,
  output [2:0] ExtOp,
  output ALUASrc,
  output MemWr
);

  wire and_4_out, and_5_out, and_6_out, and_7_out, and_8_out, and_9_out, and_10_out, and_11_out, and_12_out,
       and_13_out, and_14_out, and_15_out, and_16_out, and_17_out, and_18_out, and_19_out, and_20_out,
       and_21_out, and_23_out, and_24_out, and_25_out, and_26_out, and_27_out, not_1_out, not_2_out,
       not_3_out, not_4_out, not_5_out, not_6_out, not_7_out, not_8_out, not_9_out, not_10_out, not_11_out,
       not_12_out, not_13_out, not_14_out, not_15_out, not_16_out, not_17_out, not_18_out, not_19_out,
       not_20_out, not_21_out, not_22_out, not_23_out, not_24_out, not_25_out, not_26_out, not_27_out,
       not_28_out, not_29_out, not_30_out, not_31_out, not_32_out, not_33_out, not_34_out, not_35_out,
       not_36_out, not_37_out, not_38_out, not_39_out, not_40_out, not_41_out, not_42_out, not_43_out,
       not_44_out, not_45_out, not_46_out, not_47_out, not_48_out, not_49_out, not_50_out, not_51_out,
       not_52_out, not_53_out, not_54_out, not_55_out, not_56_out, not_57_out, not_58_out, not_59_out,
       not_60_out, not_61_out, not_62_out, not_63_out, not_64_out, not_65_out, not_66_out, or_3_out,
       or_4_out, or_5_out;

  not not_1 (not_1_out, op[2]);
  not not_2 (not_2_out, op[3]);
  and and_1 (Branch, op[0], op[1], not_1_out, not_2_out, not_3_out, op[5], op[6]);
  not not_3 (not_3_out, op[4]);
  and and_2 (Jump, op[0], op[1], op[2], op[3], not_4_out, op[5], op[6]);
  not not_4 (not_4_out, op[4]);
  not not_5 (not_5_out, op[2]);
  not not_6 (not_6_out, op[3]);
  and and_3 (MemtoReg, op[0], op[1], not_5_out, not_6_out, not_7_out, not_8_out, not_9_out);
  not not_7 (not_7_out, op[4]);
  not not_8 (not_8_out, op[5]);
  not not_9 (not_9_out, op[6]);
  not not_10 (not_10_out, op[2]);
  and and_4 (and_4_out, op[0], op[1], not_10_out, not_11_out, op[4], op[5], not_12_out);
  not not_11 (not_11_out, op[3]);
  not not_12 (not_12_out, op[6]);
  not not_13 (not_13_out, op[2]);
  not not_14 (not_14_out, op[3]);
  and and_5 (and_5_out, op[0], op[1], not_13_out, not_14_out, op[4], not_15_out, not_16_out);
  not not_15 (not_15_out, op[5]);
  not not_16 (not_16_out, op[6]);
  and and_6 (and_6_out, op[0], op[1], op[2], not_17_out, op[4], op[5], not_18_out);
  not not_17 (not_17_out, op[3]);
  not not_18 (not_18_out, op[6]);
  not not_19 (not_19_out, op[2]);
  not not_20 (not_20_out, op[3]);
  and and_7 (and_7_out, op[0], op[1], not_19_out, not_20_out, not_21_out, not_22_out, not_23_out);
  not not_21 (not_21_out, op[4]);
  not not_22 (not_22_out, op[5]);
  not not_23 (not_23_out, op[6]);
  and and_8 (and_8_out, op[0], op[1], op[2], op[3], not_24_out, op[5], op[6]);
  not not_24 (not_24_out, op[4]);
  and and_9 (and_9_out, op[0], op[1], op[2], not_25_out, op[4], op[5], not_26_out);
  not not_25 (not_25_out, op[3]);
  not not_26 (not_26_out, op[6]);
  not not_27 (not_27_out, op[2]);
  and and_10 (and_10_out, op[0], op[1], not_27_out, not_28_out, not_29_out, op[5], op[6]);
  not not_28 (not_28_out, op[3]);
  not not_29 (not_29_out, op[4]);
  not not_30 (not_30_out, op[2]);
  not not_31 (not_31_out, op[3]);
  and and_11 (and_11_out, op[0], op[1], not_30_out, not_31_out, op[4], op[5], not_32_out);
  not not_32 (not_32_out, op[6]);
  not not_33 (not_33_out, op[2]);
  and and_12 (and_12_out, op[0], op[1], not_33_out, not_34_out, op[4], not_35_out, not_36_out);
  not not_34 (not_34_out, op[3]);
  not not_35 (not_35_out, op[5]);
  not not_36 (not_36_out, op[6]);
  not not_37 (not_37_out, op[3]);
  and and_13 (and_13_out, op[0], op[1], op[2], not_37_out, op[4], op[5], not_38_out);
  not not_38 (not_38_out, op[6]);
  not not_39 (not_39_out, op[2]);
  and and_14 (and_14_out, op[0], op[1], not_39_out, not_40_out, op[4], op[5], not_41_out);
  not not_40 (not_40_out, op[3]);
  not not_41 (not_41_out, op[6]);
  not not_42 (not_42_out, op[2]);
  and and_15 (and_15_out, op[0], op[1], not_42_out, not_43_out, op[4], not_44_out, not_45_out);
  not not_43 (not_43_out, op[3]);
  not not_44 (not_44_out, op[5]);
  not not_45 (not_45_out, op[6]);
  and and_16 (and_16_out, op[0], op[1], op[2], not_46_out, op[4], op[5], not_47_out);
  not not_46 (not_46_out, op[3]);
  not not_47 (not_47_out, op[6]);
  not not_48 (not_48_out, op[2]);
  and and_17 (and_17_out, op[0], op[1], not_48_out, not_49_out, op[4], op[5], not_50_out);
  not not_49 (not_49_out, op[3]);
  not not_50 (not_50_out, op[6]);
  not not_51 (not_51_out, op[2]);
  not not_52 (not_52_out, op[3]);
  and and_18 (and_18_out, op[0], op[1], not_51_out, not_52_out, op[4], not_53_out, not_54_out);
  not not_53 (not_53_out, op[5]);
  not not_54 (not_54_out, op[6]);
  not not_55 (not_55_out, op[3]);
  and and_19 (and_19_out, op[0], op[1], op[2], not_55_out, op[4], op[5], not_56_out);
  not not_56 (not_56_out, op[6]);
  not not_57 (not_57_out, op[4]);
  and and_20 (and_20_out, not_57_out, not_58_out);
  not not_58 (not_58_out, op[6]);
  and and_21 (and_21_out, op[2], not_59_out);
  not not_59 (not_59_out, op[3]);
  not not_60 (not_60_out, op[6]);
  and and_22 (MemWr, not_60_out, op[5], not_61_out);
  not not_61 (not_61_out, op[4]);
  or or_1 (RegWr, and_4_out, and_5_out, and_6_out, and_7_out, and_8_out);
  or or_2 (ALUctr_3_0[3], and_9_out, and_10_out);
  or or_3 (or_3_out, and_11_out, and_12_out);
  or or_4 (or_4_out, and_14_out, and_15_out);
  or or_5 (or_5_out, and_17_out, and_18_out);
  not not_62 (not_62_out, op[5]);
  not not_63 (not_63_out, funct3[1]);
  not not_64 (not_64_out, op[3]);
  not not_65 (not_65_out, op[3]);
  not not_66 (not_66_out, op[2]);
  and and_23 (and_23_out, or_3_out, funct3[2]);
  or or_6 (ALUctr_3_0[2], and_23_out, and_13_out);
  and and_24 (and_24_out, funct3[1], or_4_out);
  or or_7 (ALUctr_3_0[1], and_24_out, and_16_out);
  and and_25 (and_25_out, funct3[0], or_5_out);
  or or_8 (ALUctr_3_0[0], and_25_out, and_19_out);
  or or_9 (ALUBSrc_1_0[1], and_20_out, not_62_out, and_21_out);
  and and_26 (and_26_out, not_63_out, not_64_out);
  and and_27 (and_27_out, not_65_out, op[2]);
  and and_28 (ExtOp[1], not_66_out, op[5]);
  or or_10 (ExtOp[0], and_26_out, and_27_out);

  assign ALUASrc = op[3];
  assign ALUBSrc_1_0[0] = op[3];
  assign ExtOp[2] = op[3];
endmodule

module \指令解析  (
  input  [31:0] \输入指令 ,
  input  [2:0] ExtOp,
  output [6:0] funct7,
  output [6:0] op,
  output [2:0] funct3,
  output [4:0] Rs2,
  output [31:0] imm,
  output [4:0] Rs1,
  output [4:0] Rd
);

  \立即数扩展器  \u_立即数扩展器_1  (.Instr(\输入指令 ), .ExtOp(ExtOp), .imm(imm));

  assign funct3 = \输入指令 [14:12];
  assign funct7 = \输入指令 [31:25];
  assign op = \输入指令 [6:0];
  assign Rd = \输入指令 [11:7];
  assign Rs1 = \输入指令 [19:15];
  assign Rs2 = \输入指令 [24:20];
endmodule
