// Logisim project LAB 6.circ as structural Verilog: 13 circuits, main circuit ALUCtr
module ALUCtr (
  input  [3:0] Cin,
  output SUBctr,
  output SIGctr,
  output [1:0] OPctr
);

  wire and_1_out, not_2_out, not_3_out;

  or or_1 (SUBctr, Cin[1], Cin[3]);
  not not_1 (SIGctr, Cin[0]);
  not not_2 (not_2_out, Cin[2]);
  not not_3 (not_3_out, Cin[3]);
  and and_1 (and_1_out, not_2_out, Cin[1]);
  and and_2 (OPctr[0], not_3_out, Cin[1]);
  or or_2 (OPctr[1], Cin[0], and_1_out);
endmodule

module \指令分解  (
  input  [31:0] \输入指令 ,
  input  [2:0] Extop,
  output [6:0] op,
  output [4:0] rd,
  output [2:0] funct3,
  output [4:0] rs1,
  output [4:0] rs2,
  output [6:0] funct7,
  output [31:0] imm
);

  InstrToimm instrtoimm_1 (.INSTRUCTION(\输入指令 ), .Imm(imm), .EXTOP(Extop));

  assign funct3 = \输入指令 [14:12];
  assign funct7 = \输入指令 [31:25];
  assign op = \输入指令 [6:0];
  assign rd = \输入指令 [11:7];
  assign rs1 = \输入指令 [19:15];
  assign rs2 = \输入指令 [24:20];
endmodule

module InstrToimm (
  input  [31:0] INSTRUCTION,
  input  [2:0] EXTOP,
  output [31:0] Imm
);

  wire [11:0] bit_extender_4_out;
  wire [19:0] bit_extender_1_out, bit_extender_2_out, bit_extender_3_out;

  assign bit_extender_1_out = {{19{INSTRUCTION[31]}}, INSTRUCTION[31]};  // Bit_Extender bit_extender_1
  assign bit_extender_2_out = {{19{INSTRUCTION[31]}}, INSTRUCTION[31]};  // Bit_Extender bit_extender_2
  assign bit_extender_3_out = {{19{INSTRUCTION[31]}}, INSTRUCTION[31]};  // Bit_Extender bit_extender_3
  assign bit_extender_4_out = {{11{INSTRUCTION[31]}}, INSTRUCTION[31]};  // Bit_Extender bit_extender_4
  Multiplexer #(.select(3), .width(32), .enable("false")) multiplexer_1 (
    .in0({bit_extender_1_out, INSTRUCTION[31:20]}), .in1({INSTRUCTION[31:12], {12{1'b0}}}),
    .in2({bit_extender_2_out, INSTRUCTION[31:25], INSTRUCTION[11:7]}),
    .in3({bit_extender_3_out, INSTRUCTION[7], INSTRUCTION[30:25], INSTRUCTION[11:8], 1'b0}),
    .in4({bit_extender_4_out, INSTRUCTION[19:12], INSTRUCTION[20], INSTRUCTION[30:21], 1'b0}),
    .in5({32{1'b0}}), .in6({32{1'b0}}), .in7({32{1'b0}}), .out(Imm), .sel(EXTOP));

  // Notes on the sheet:
  //   I
  //   U
  //   S
  //   B
  //   J
endmodule

// 控制器
module \控制部件  (
  input  [6:0] OP_6_0,
  input  [2:0] funct3,
  output REGwr,
  output MEMTOREG,
  output MEMWR,
  output BRANCH,
  output JUMP,
  output [3:0] ALUctr_3_0,
  output ALUASrc,
  output [1:0] ALUBSrc,
  output [2:0] EXTOP
);

  wire and_1_out, and_2_out, and_3_out, and_4_out, and_5_out, and_6_out, and_7_out, \I型_out , Lui_out,
       not_1_out, not_2_out, not_3_out, or_1_out, or_2_out, \R型_out ;

  and \R型  (\R型_out , ~OP_6_0[6], OP_6_0[5], OP_6_0[4], ~OP_6_0[3], ~OP_6_0[2], OP_6_0[1], OP_6_0[0]);  // AND_Gate
  and \I型  (\I型_out , ~OP_6_0[6], ~OP_6_0[5], OP_6_0[4], ~OP_6_0[3], ~OP_6_0[2], OP_6_0[1], OP_6_0[0]);  // AND_Gate
  or or_1 (or_1_out, \R型_out , \I型_out );
  and and_1 (and_1_out, or_1_out, funct3[2]);
  and and_2 (and_2_out, or_1_out, funct3[1]);
  and and_3 (and_3_out, or_1_out, funct3[0]);
  and Lui (Lui_out, ~OP_6_0[6], OP_6_0[5], OP_6_0[4], ~OP_6_0[3], OP_6_0[2], OP_6_0[1], OP_6_0[0]);  // AND_Gate
  and Load (MEMTOREG, ~OP_6_0[6], ~OP_6_0[5], ~OP_6_0[4], ~OP_6_0[3], ~OP_6_0[2], OP_6_0[1], OP_6_0[0]);  // AND_Gate
  and and_4 (and_4_out, \I型_out , funct3[1], funct3[2]);
  and Store (MEMWR, ~OP_6_0[6], OP_6_0[5], ~OP_6_0[4], ~OP_6_0[3], ~OP_6_0[2], OP_6_0[1], OP_6_0[0]);  // AND_Gate
  or or_2 (or_2_out, MEMTOREG, MEMWR);
  and \B型  (BRANCH, OP_6_0[6], OP_6_0[5], ~OP_6_0[4], ~OP_6_0[3], ~OP_6_0[2], OP_6_0[1], OP_6_0[0]);  // AND_Gate
  not not_1 (not_1_out, funct3[0]);
  not not_2 (not_2_out, funct3[1]);
  not not_3 (not_3_out, funct3[2]);
  and \J型  (ALUASrc, OP_6_0[6], OP_6_0[5], ~OP_6_0[4], OP_6_0[3], OP_6_0[2], OP_6_0[1], OP_6_0[0]);  // AND_Gate
  and and_5 (and_5_out, or_2_out, funct3[1]);
  and and_6 (and_6_out, MEMWR, funct3[1]);
  and and_7 (and_7_out, BRANCH, not_1_out, not_2_out, not_3_out);
  or or_3 (REGwr, \R型_out , \I型_out , Lui_out, MEMTOREG, ALUASrc);
  or or_4 (ALUctr_3_0[3], Lui_out, BRANCH);
  or or_5 (ALUctr_3_0[2], Lui_out, and_1_out);
  or or_6 (ALUctr_3_0[1], Lui_out, and_2_out);
  or or_7 (ALUctr_3_0[0], Lui_out, and_3_out);
  or or_8 (ALUBSrc[1], and_5_out, Lui_out, and_4_out);
  or or_9 (EXTOP[1], and_6_out, and_7_out);
  or or_10 (EXTOP[0], Lui_out, and_7_out);

  assign ALUBSrc[0] = ALUASrc;
  assign EXTOP[2] = ALUASrc;
  assign JUMP = ALUASrc;
endmodule

module CPU (
);

  wire alu_1_zero, and_1_out, button_1_out, button_2_out, clock_1_out, clock_2_out, clock_3_out, not_1_out,
       or_1_out, \控制部件_1_aluasrc , \控制部件_1_branch , \控制部件_1_jump , \控制部件_1_memtoreg , \控制部件_1_memwr ,
       \控制部件_1_regwr ;
  wire [1:0] \控制部件_1_alubsrc ;
  wire [2:0] \指令分解_1_funct3 , \控制部件_1_extop ;
  wire [3:0] \控制部件_1_aluctr_3_0 ;
  wire [4:0] \指令分解_1_rd , \指令分解_1_rs1 , \指令分解_1_rs2 ;
  wire [6:0] \指令分解_1_op ;
  wire [11:0] pc_q_2;
  wire [31:0] adder_1_out, alu_1_result, multiplexer_1_out, multiplexer_2_out, multiplexer_3_out,
       multiplexer_4_out, pc_q, \寄存器_1_busa , \寄存器_1_busb , \指令分解_1_imm , \指令存储器_data , \数据存储器_data ;

  Clock clock_1 (.out(clock_1_out));
  Clock clock_2 (.out(clock_2_out));
  \指令分解  \u_指令分解_1  (
    .\输入指令 (\指令存储器_data ), .Extop(\控制部件_1_extop ), .op(\指令分解_1_op ), .rd(\指令分解_1_rd ),
    .funct3(\指令分解_1_funct3 ), .rs1(\指令分解_1_rs1 ), .rs2(\指令分解_1_rs2 ), .imm(\指令分解_1_imm ));  // open: funct7
  ROM #(.addrWidth(12), .dataWidth(32), .Select("low")) \u_指令存储器  (.addr(pc_q_2), .data(\指令存储器_data ));
  \寄存器  \u_寄存器_1  (
    .busA(\寄存器_1_busa ), .RW(\指令分解_1_rd ), .busW(multiplexer_4_out), .busB(\寄存器_1_busb ), .RB(\指令分解_1_rs2 ),
    .RA(\指令分解_1_rs1 ), .WE(\控制部件_1_regwr ), .in_6(clock_2_out));
  Register #(.width(32), .trigger("falling"), .Select("low")) pc (
    .D(adder_1_out), .Q({pc_q[31:14], pc_q_2, pc_q[1:0]}), .clk(clock_1_out), .clr(button_1_out));  // open: en
  Button button_1 (.out(button_1_out));
  Multiplexer #(.width(32), .enable("false")) multiplexer_1 (
    .in0(\寄存器_1_busa ), .in1({pc_q[31:14], pc_q_2, pc_q[1:0]}), .out(multiplexer_1_out),
    .sel(\控制部件_1_aluasrc ));
  Multiplexer #(.select(2), .width(32), .enable("false")) multiplexer_2 (
    .in0(\寄存器_1_busb ), .in1(32'h4), .in2(\指令分解_1_imm ), .out(multiplexer_2_out), .sel(\控制部件_1_alubsrc ));  // open: in3
  Adder #(.width(32)) adder_1 (
    .a({pc_q[31:14], pc_q_2, pc_q[1:0]}), .b(multiplexer_3_out), .out(adder_1_out));  // open: cin, cout
  Multiplexer #(.width(32), .enable("false")) multiplexer_3 (
    .in0(32'h4), .in1(\指令分解_1_imm ), .out(multiplexer_3_out), .sel(or_1_out));
  ALU alu_1 (
    .A(multiplexer_1_out), .B(multiplexer_2_out), .ALUctr(\控制部件_1_aluctr_3_0 ), .Zero(alu_1_zero),
    .Result(alu_1_result));
  or or_1 (or_1_out, and_1_out, \控制部件_1_jump );
  and and_1 (and_1_out, alu_1_zero, \控制部件_1_branch );
  Clock clock_3 (.out(clock_3_out));
  RAM #(.addrWidth(12), .dataWidth(32), .bus("separate"), .Select("high")) \u_数据存储器  (
    .addr(alu_1_result[13:2]), .din(\寄存器_1_busb ), .data(\数据存储器_data ), .str(\控制部件_1_memwr ),
    .clk(clock_3_out), .ld(not_1_out), .clr(button_2_out));  // open: sel
  not not_1 (not_1_out, \控制部件_1_memwr );
  Button button_2 (.out(button_2_out));
  \控制部件  \u_控制部件_1  (
    .REGwr(\控制部件_1_regwr ), .MEMTOREG(\控制部件_1_memtoreg ), .MEMWR(\控制部件_1_memwr ), .BRANCH(\控制部件_1_branch ),
    .JUMP(\控制部件_1_jump ), .ALUctr_3_0(\控制部件_1_aluctr_3_0 ), .ALUASrc(\控制部件_1_aluasrc ),
    .ALUBSrc(\控制部件_1_alubsrc ), .EXTOP(\控制部件_1_extop ), .OP_6_0(\指令分解_1_op ), .funct3(\指令分解_1_funct3 ));
  Multiplexer #(.width(32), .enable("false")) multiplexer_4 (
    .in0(alu_1_result), .in1(\数据存储器_data ), .out(multiplexer_4_out), .sel(\控制部件_1_memtoreg ));

  // Notes on the sheet:
  //   contents of 指令存储器 (hex, n*v repeats v):
  //   2083 8133 106213 406293 fff06313 4410663 106193 406393 806413 21b5b3 2058063 3a483 42503 a4b5b3
  //   458c63 a3a023 942023 c0006f 610133 fc9ff06f 4181b3 5383b3 540433 fc9ff06f 6f
endmodule

module \寄存器  (
  input  [4:0] RW,
  input  [31:0] busW,
  input  [4:0] RB,
  input  [4:0] RA,
  input  WE,
  input  in_6,
  output [31:0] busA,
  output [31:0] busB
);

  wire and_1_out, and_2_out, and_3_out, and_4_out, and_5_out, and_6_out, and_7_out, and_8_out, and_9_out,
       and_10_out, and_11_out, and_12_out, and_13_out, and_14_out, and_15_out, and_16_out, and_17_out,
       and_18_out, and_19_out, and_20_out, and_21_out, and_22_out, and_23_out, and_24_out, and_25_out,
       and_26_out, and_27_out, and_28_out, and_29_out, and_30_out, and_31_out, and_32_out, decoder_1_out0,
       decoder_1_out1, decoder_1_out2, decoder_1_out3, decoder_1_out4, decoder_1_out5, decoder_1_out6,
       decoder_1_out7, decoder_1_out8, decoder_1_out9, decoder_1_out10, decoder_1_out11, decoder_1_out12,
       decoder_1_out13, decoder_1_out14, decoder_1_out15, decoder_1_out16, decoder_1_out17, decoder_1_out18,
       decoder_1_out19, decoder_1_out20, decoder_1_out21, decoder_1_out22, decoder_1_out23, decoder_1_out24,
       decoder_1_out25, decoder_1_out26, decoder_1_out27, decoder_1_out28, decoder_1_out29, decoder_1_out30,
       decoder_1_out31;
  wire [31:0] \寄存器0_q , \寄存器1_q , \寄存器2_q , \寄存器3_q , \寄存器4_q , \寄存器5_q , \寄存器6_q , \寄存器7_q , \寄存器8_q ,
       \寄存器9_q , \寄存器10_q , \寄存器11_q , \寄存器12_q , \寄存器13_q , \寄存器14_q , \寄存器15_q , \寄存器16_q , \寄存器17_q ,
       \寄存器18_q , \寄存器19_q , \寄存器20_q , \寄存器21_q , \寄存器22_q , \寄存器23_q , \寄存器24_q , \寄存器25_q , \寄存器26_q ,
       \寄存器27_q , \寄存器28_q , \寄存器29_q , \寄存器30_q , \寄存器31_q ;

  Decoder #(.select(5), .enable("false")) decoder_1 (
    .out0(decoder_1_out0), .out1(decoder_1_out1), .out2(decoder_1_out2), .out3(decoder_1_out3),
    .out4(decoder_1_out4), .out5(decoder_1_out5), .out6(decoder_1_out6), .out7(decoder_1_out7),
    .out8(decoder_1_out8), .out9(decoder_1_out9), .out10(decoder_1_out10), .out11(decoder_1_out11),
    .out12(decoder_1_out12), .out13(decoder_1_out13), .out14(decoder_1_out14), .out15(decoder_1_out15),
    .out16(decoder_1_out16), .out17(decoder_1_out17), .out18(decoder_1_out18), .out19(decoder_1_out19),
    .out20(decoder_1_out20), .out21(decoder_1_out21), .out22(decoder_1_out22), .out23(decoder_1_out23),
    .out24(decoder_1_out24), .out25(decoder_1_out25), .out26(decoder_1_out26), .out27(decoder_1_out27),
    .out28(decoder_1_out28), .out29(decoder_1_out29), .out30(decoder_1_out30), .out31(decoder_1_out31),
    .sel(RW));
  and and_1 (and_1_out, WE, in_6, decoder_1_out0);
  and and_2 (and_2_out, WE, in_6, decoder_1_out1);
  and and_3 (and_3_out, WE, in_6, decoder_1_out2);
  and and_4 (and_4_out, WE, in_6, decoder_1_out3);
  and and_5 (and_5_out, WE, in_6, decoder_1_out4);
  and and_6 (and_6_out, WE, in_6, decoder_1_out5);
  and and_7 (and_7_out, WE, in_6, decoder_1_out6);
  and and_8 (and_8_out, WE, in_6, decoder_1_out7);
  and and_9 (and_9_out, decoder_1_out8, in_6, WE);
  and and_10 (and_10_out, decoder_1_out9, in_6, WE);
  and and_11 (and_11_out, decoder_1_out10, in_6, WE);
  and and_12 (and_12_out, decoder_1_out11, in_6, WE);
  and and_13 (and_13_out, decoder_1_out12, in_6, WE);
  and and_14 (and_14_out, decoder_1_out13, in_6, WE);
  and and_15 (and_15_out, decoder_1_out14, in_6, WE);
  and and_16 (and_16_out, in_6, decoder_1_out15, WE);
  and and_17 (and_17_out, decoder_1_out16, in_6, WE);
  and and_18 (and_18_out, decoder_1_out17, in_6, WE);
  and and_19 (and_19_out, decoder_1_out18, in_6, WE);
  and and_20 (and_20_out, decoder_1_out19, in_6, WE);
  and and_21 (and_21_out, decoder_1_out20, in_6, WE);
  and and_22 (and_22_out, decoder_1_out21, in_6, WE);
  and and_23 (and_23_out, decoder_1_out22, in_6, WE);
  and and_24 (and_24_out, decoder_1_out23, in_6, WE);
  and and_25 (and_25_out, decoder_1_out24, in_6, WE);
  and and_26 (and_26_out, decoder_1_out25, in_6, WE);
  and and_27 (and_27_out, decoder_1_out26, in_6, WE);
  and and_28 (and_28_out, decoder_1_out27, in_6, WE);
  and and_29 (and_29_out, decoder_1_out28, in_6, WE);
  and and_30 (and_30_out, decoder_1_out29, in_6, WE);
  and and_31 (and_31_out, decoder_1_out30, in_6, WE);
  and and_32 (and_32_out, decoder_1_out31, in_6, WE);
  Register #(.width(32), .Select("low")) \u_寄存器0  (.D(busW), .en(1'b0), .Q(\寄存器0_q ), .clk(and_1_out));  // open: clr
  Register #(.width(32), .Select("low")) \u_寄存器1  (.D(busW), .Q(\寄存器1_q ), .clk(and_2_out));  // open: en, clr
  Register #(.width(32), .Select("low")) \u_寄存器2  (.D(busW), .Q(\寄存器2_q ), .clk(and_3_out));  // open: en, clr
  Register #(.width(32), .Select("low")) \u_寄存器3  (.D(busW), .Q(\寄存器3_q ), .clk(and_4_out));  // open: en, clr
  Register #(.width(32), .Select("low")) \u_寄存器4  (.D(busW), .Q(\寄存器4_q ), .clk(and_5_out));  // open: en, clr
  Register #(.width(32), .Select("low")) \u_寄存器5  (.D(busW), .Q(\寄存器5_q ), .clk(and_6_out));  // open: en, clr
  Register #(.width(32), .Select("low")) \u_寄存器6  (.D(busW), .Q(\寄存器6_q ), .clk(and_7_out));  // open: en, clr
  Register #(.width(32), .Select("low")) \u_寄存器7  (.D(busW), .Q(\寄存器7_q ), .clk(and_8_out));  // open: en, clr
  Register #(.width(32), .Select("low")) \u_寄存器8  (.D(busW), .Q(\寄存器8_q ), .clk(and_9_out));  // open: en, clr
  Register #(.width(32), .Select("low")) \u_寄存器9  (.D(busW), .Q(\寄存器9_q ), .clk(and_10_out));  // open: en, clr
  Register #(.width(32), .Select("low")) \u_寄存器10  (.D(busW), .Q(\寄存器10_q ), .clk(and_11_out));  // open: en, clr
  Register #(.width(32), .Select("low")) \u_寄存器11  (.D(busW), .Q(\寄存器11_q ), .clk(and_12_out));  // open: en, clr
  Register #(.width(32), .Select("low")) \u_寄存器12  (.D(busW), .Q(\寄存器12_q ), .clk(and_13_out));  // open: en, clr
  Register #(.width(32), .Select("low")) \u_寄存器13  (.D(busW), .Q(\寄存器13_q ), .clk(and_14_out));  // open: en, clr
  Register #(.width(32), .Select("low")) \u_寄存器14  (.D(busW), .Q(\寄存器14_q ), .clk(and_15_out));  // open: en, clr
  Register #(.width(32), .Select("low")) \u_寄存器15  (.D(busW), .Q(\寄存器15_q ), .clk(and_16_out));  // open: en, clr
  Register #(.width(32), .Select("low")) \u_寄存器16  (.D(busW), .Q(\寄存器16_q ), .clk(and_17_out));  // open: en, clr
  Register #(.width(32), .Select("low")) \u_寄存器17  (.D(busW), .Q(\寄存器17_q ), .clk(and_18_out));  // open: en, clr
  Register #(.width(32), .Select("low")) \u_寄存器18  (.D(busW), .Q(\寄存器18_q ), .clk(and_19_out));  // open: en, clr
  Register #(.width(32), .Select("low")) \u_寄存器19  (.D(busW), .Q(\寄存器19_q ), .clk(and_20_out));  // open: en, clr
  Register #(.width(32), .Select("low")) \u_寄存器20  (.D(busW), .Q(\寄存器20_q ), .clk(and_21_out));  // open: en, clr
  Register #(.width(32), .Select("low")) \u_寄存器21  (.D(busW), .Q(\寄存器21_q ), .clk(and_22_out));  // open: en, clr
  Register #(.width(32), .Select("low")) \u_寄存器22  (.D(busW), .Q(\寄存器22_q ), .clk(and_23_out));  // open: en, clr
  Register #(.width(32), .Select("low")) \u_寄存器23  (.D(busW), .Q(\寄存器23_q ), .clk(and_24_out));  // open: en, clr
  Register #(.width(32), .Select("low")) \u_寄存器24  (.D(busW), .Q(\寄存器24_q ), .clk(and_25_out));  // open: en, clr
  Register #(.width(32), .Select("low")) \u_寄存器25  (.D(busW), .Q(\寄存器25_q ), .clk(and_26_out));  // open: en, clr
  Register #(.width(32), .Select("low")) \u_寄存器26  (.D(busW), .Q(\寄存器26_q ), .clk(and_27_out));  // open: en, clr
  Register #(.width(32), .Select("low")) \u_寄存器27  (.D(busW), .Q(\寄存器27_q ), .clk(and_28_out));  // open: en, clr
  Register #(.width(32), .Select("low")) \u_寄存器28  (.D(busW), .Q(\寄存器28_q ), .clk(and_29_out));  // open: en, clr
  Register #(.width(32), .Select("low")) \u_寄存器29  (.D(busW), .Q(\寄存器29_q ), .clk(and_30_out));  // open: en, clr
  Register #(.width(32), .Select("low")) \u_寄存器30  (.D(busW), .Q(\寄存器30_q ), .clk(and_31_out));  // open: en, clr
  Register #(.width(32), .Select("low")) \u_寄存器31  (.D(busW), .Q(\寄存器31_q ), .clk(and_32_out));  // open: en, clr
  Multiplexer #(.select(5), .width(32), .enable("false")) multiplexer_1 (
    .in0(\寄存器0_q ), .in1(\寄存器1_q ), .in2(\寄存器2_q ), .in3(\寄存器3_q ), .in4(\寄存器4_q ), .in5(\寄存器5_q ),
    .in6(\寄存器6_q ), .in7(\寄存器7_q ), .in8(\寄存器8_q ), .in9(\寄存器9_q ), .in10(\寄存器10_q ), .in11(\寄存器11_q ),
    .in12(\寄存器12_q ), .in13(\寄存器13_q ), .in14(\寄存器14_q ), .in15(\寄存器15_q ), .in16(\寄存器16_q ),
    .in17(\寄存器17_q ), .in18(\寄存器18_q ), .in19(\寄存器19_q ), .in20(\寄存器20_q ), .in21(\寄存器21_q ),
    .in22(\寄存器22_q ), .in23(\寄存器23_q ), .in24(\寄存器24_q ), .in25(\寄存器25_q ), .in26(\寄存器26_q ),
    .in27(\寄存器27_q ), .in28(\寄存器28_q ), .in29(\寄存器29_q ), .in30(\寄存器30_q ), .in31(\寄存器31_q ), .out(busA),
    .sel(RA));
  Multiplexer #(.select(5), .width(32), .enable("false")) multiplexer_2 (
    .in0(\寄存器0_q ), .in1(\寄存器1_q ), .in2(\寄存器2_q ), .in3(\寄存器3_q ), .in4(\寄存器4_q ), .in5(\寄存器5_q ),
    .in6(\寄存器6_q ), .in7(\寄存器7_q ), .in8(\寄存器8_q ), .in9(\寄存器9_q ), .in10(\寄存器10_q ), .in11(\寄存器11_q ),
    .in12(\寄存器12_q ), .in13(\寄存器13_q ), .in14(\寄存器14_q ), .in15(\寄存器15_q ), .in16(\寄存器16_q ),
    .in17(\寄存器17_q ), .in18(\寄存器18_q ), .in19(\寄存器19_q ), .in20(\寄存器20_q ), .in21(\寄存器21_q ),
    .in22(\寄存器22_q ), .in23(\寄存器23_q ), .in24(\寄存器24_q ), .in25(\寄存器25_q ), .in26(\寄存器26_q ),
    .in27(\寄存器27_q ), .in28(\寄存器28_q ), .in29(\寄存器29_q ), .in30(\寄存器30_q ), .in31(\寄存器31_q ), .out(busB),
    .sel(RB));
endmodule

module CLA (
  input  B3,
  input  A3,
  input  B2,
  input  A2,
  input  B1,
  input  A1,
  input  B0,
  input  A0,
  input  C0,
  output C4,
  output S3,
  output S2,
  output S1,
  output S0
);

  wire and_1_out, and_2_out, and_3_out, and_4_out, and_6_out, and_7_out, and_8_out, nand_1_out, nand_2_out,
       nand_3_out, nand_4_out, nor_1_out, nor_2_out, nor_3_out, nor_4_out, not_1_out, not_2_out, not_3_out,
       not_4_out, not_5_out, not_6_out, not_7_out, not_8_out, not_9_out, not_10_out, not_11_out, not_12_out,
       not_13_out, not_14_out, not_15_out, not_16_out, not_17_out, not_18_out, not_19_out, not_20_out,
       not_21_out, not_22_out, not_23_out, not_24_out, not_25_out, not_26_out, not_27_out, not_28_out,
       not_29_out, not_30_out, not_31_out, not_32_out, not_33_out, not_34_out, not_35_out, not_36_out,
       not_37_out, not_38_out, not_39_out, not_40_out, or_1_out, or_2_out, or_3_out, or_4_out, or_5_out,
       or_6_out, or_7_out, or_8_out, or_9_out, or_10_out;

  nand nand_1 (nand_1_out, B3, A3);
  nor nor_1 (nor_1_out, B3, A3);
  nand nand_2 (nand_2_out, B2, A2);
  nor nor_2 (nor_2_out, B2, A2);
  nand nand_3 (nand_3_out, B1, A1);
  nor nor_3 (nor_3_out, B1, A1);
  nand nand_4 (nand_4_out, B0, A0);
  nor nor_4 (nor_4_out, B0, A0);
  not not_1 (not_1_out, C0);
  not not_2 (not_2_out, nor_1_out);
  not not_3 (not_3_out, nor_2_out);
  not not_4 (not_4_out, nand_1_out);
  not not_5 (not_5_out, nor_3_out);
  not not_6 (not_6_out, nand_1_out);
  not not_7 (not_7_out, nand_2_out);
  not not_8 (not_8_out, nor_4_out);
  not not_9 (not_9_out, nand_1_out);
  not not_10 (not_10_out, nand_2_out);
  not not_11 (not_11_out, nand_3_out);
  not not_12 (not_12_out, nand_1_out);
  not not_13 (not_13_out, nand_2_out);
  not not_14 (not_14_out, nand_3_out);
  not not_15 (not_15_out, nand_4_out);
  not not_16 (not_16_out, not_1_out);
  not not_17 (not_17_out, nor_1_out);
  not not_18 (not_18_out, nor_2_out);
  not not_19 (not_19_out, nor_3_out);
  not not_20 (not_20_out, nand_2_out);
  not not_21 (not_21_out, nor_4_out);
  not not_22 (not_22_out, nand_2_out);
  not not_23 (not_23_out, nand_3_out);
  not not_24 (not_24_out, nand_2_out);
  not not_25 (not_25_out, nand_3_out);
  not not_26 (not_26_out, nand_4_out);
  not not_27 (not_27_out, not_1_out);
  not not_28 (not_28_out, nor_2_out);
  not not_29 (not_29_out, nor_3_out);
  not not_30 (not_30_out, nor_4_out);
  not not_31 (not_31_out, nand_3_out);
  not not_32 (not_32_out, nand_3_out);
  not not_33 (not_33_out, nand_4_out);
  not not_34 (not_34_out, not_1_out);
  not not_35 (not_35_out, nor_3_out);
  not not_36 (not_36_out, nor_4_out);
  not not_37 (not_37_out, nand_4_out);
  not not_38 (not_38_out, not_1_out);
  not not_39 (not_39_out, nor_4_out);
  not not_40 (not_40_out, not_1_out);
  or or_1 (or_1_out, not_3_out, not_4_out);
  or or_2 (or_2_out, not_5_out, not_6_out, not_7_out);
  or or_3 (or_3_out, not_8_out, not_9_out, not_10_out, not_11_out);
  or or_4 (or_4_out, not_12_out, not_13_out, not_14_out, not_15_out, not_16_out);
  and and_1 (and_1_out, nand_1_out, not_17_out);
  or or_5 (or_5_out, not_19_out, not_20_out);
  or or_6 (or_6_out, not_21_out, not_22_out, not_23_out);
  or or_7 (or_7_out, not_24_out, not_25_out, not_26_out, not_27_out);
  and and_2 (and_2_out, nand_2_out, not_28_out);
  or or_8 (or_8_out, not_30_out, not_31_out);
  or or_9 (or_9_out, not_32_out, not_33_out, not_34_out);
  and and_3 (and_3_out, nand_3_out, not_35_out);
  or or_10 (or_10_out, not_37_out, not_38_out);
  and and_4 (and_4_out, nand_4_out, not_39_out);
  and and_5 (C4, not_2_out, or_1_out, or_2_out, or_3_out, or_4_out);
  and and_6 (and_6_out, not_18_out, or_5_out, or_6_out, or_7_out);
  and and_7 (and_7_out, not_29_out, or_8_out, or_9_out);
  and and_8 (and_8_out, not_36_out, or_10_out);
  xor xor_1 (S3, and_1_out, and_6_out);
  xor xor_2 (S2, and_2_out, and_7_out);
  xor xor_3 (S1, and_3_out, and_8_out);
  xor xor_4 (S0, and_4_out, not_40_out);
endmodule

module CLU (
  input  X3,
  input  Y3,
  input  X2,
  input  Y2,
  input  X1,
  input  Y1,
  input  X0,
  input  Y0,
  input  C0,
  output C4,
  output C3,
  output C2,
  output C1
);

  wire and_1_out, and_2_out, and_3_out, and_4_out, and_5_out, and_6_out, and_7_out, and_8_out, and_9_out,
       and_10_out, G0_out, G1_out, G2_out, G3_out, P0_out, P1_out, P2_out, P3_out;

  and G3 (G3_out, X3, Y3);
  or P3 (P3_out, X3, Y3);
  and G2 (G2_out, X2, Y2);
  or P2 (P2_out, X2, Y2);
  and G1 (G1_out, X1, Y1);
  or P1 (P1_out, X1, Y1);
  and G0 (G0_out, X0, Y0);
  or P0 (P0_out, X0, Y0);
  and and_1 (and_1_out, P3_out, P2_out, P1_out, P0_out, C0);
  and and_2 (and_2_out, P3_out, P2_out, P1_out, G0_out);
  and and_3 (and_3_out, G1_out, P2_out, P3_out);
  and and_4 (and_4_out, P3_out, G2_out);
  and and_5 (and_5_out, P2_out, P1_out, P0_out, C0);
  and and_6 (and_6_out, P2_out, P1_out, G0_out);
  and and_7 (and_7_out, P2_out, G1_out);
  and and_8 (and_8_out, P1_out, P0_out, C0);
  and and_9 (and_9_out, P1_out, G0_out);
  and and_10 (and_10_out, P0_out, C0);
  or or_1 (C4, and_1_out, and_2_out, G3_out, and_3_out, and_4_out);
  or or_2 (C3, and_5_out, G2_out, and_6_out, and_7_out);
  or or_3 (C2, G1_out, and_8_out, and_9_out);
  or or_4 (C1, G0_out, and_10_out);
endmodule

module \_4位加法器  (
  input  B3,
  input  A3,
  input  B2,
  input  A2,
  input  B1,
  input  A1,
  input  B0,
  input  A0,
  input  C0,
  output C4,
  output S3,
  output S2,
  output S1,
  output S0,
  output Gg,
  output Pg
);

  wire and_1_out, and_2_out, and_3_out, and_5_out, and_6_out, and_7_out, and_8_out, and_10_out, and_11_out,
       and_12_out, nand_1_out, nand_2_out, nand_3_out, nand_4_out, nor_1_out, nor_2_out, nor_3_out,
       nor_4_out, not_1_out, not_2_out, not_3_out, not_4_out, not_5_out, not_6_out, not_7_out, not_8_out,
       not_9_out, not_10_out, not_11_out, not_12_out, not_13_out, not_14_out, not_15_out, not_16_out,
       not_17_out, not_18_out, not_19_out, not_20_out, not_21_out, not_22_out, not_23_out, not_24_out,
       not_25_out, not_26_out, not_27_out, not_28_out, not_29_out, not_30_out, not_31_out, not_32_out,
       not_33_out, not_34_out, not_35_out, not_36_out, not_37_out, not_38_out, not_39_out, not_40_out,
       not_41_out, not_42_out, not_43_out, not_44_out, not_45_out, not_46_out, not_47_out, not_48_out,
       not_49_out, not_50_out, not_51_out, not_52_out, not_53_out, not_54_out, or_2_out, or_3_out, or_4_out,
       or_5_out, or_6_out, or_7_out, or_8_out, or_9_out, or_10_out, or_11_out;

  nand nand_1 (nand_1_out, B3, A3);
  nor nor_1 (nor_1_out, B3, A3);
  nand nand_2 (nand_2_out, B2, A2);
  nor nor_2 (nor_2_out, B2, A2);
  nand nand_3 (nand_3_out, B1, A1);
  nor nor_3 (nor_3_out, B1, A1);
  nand nand_4 (nand_4_out, B0, A0);
  nor nor_4 (nor_4_out, B0, A0);
  not not_1 (not_1_out, C0);
  not not_2 (not_2_out, nor_1_out);
  not not_3 (not_3_out, nor_2_out);
  and and_1 (and_1_out, not_2_out, not_3_out, not_4_out, not_5_out);
  not not_4 (not_4_out, nor_3_out);
  not not_5 (not_5_out, nand_4_out);
  not not_6 (not_6_out, nor_1_out);
  not not_7 (not_7_out, nor_2_out);
  and and_2 (and_2_out, not_6_out, not_7_out, not_8_out);
  not not_8 (not_8_out, nand_3_out);
  not not_9 (not_9_out, nor_1_out);
  and and_3 (and_3_out, not_9_out, not_10_out);
  not not_10 (not_10_out, nand_2_out);
  not not_11 (not_11_out, nor_1_out);
  not not_12 (not_12_out, nor_2_out);
  and and_4 (Pg, not_11_out, not_12_out, not_13_out, not_14_out);
  not not_13 (not_13_out, nor_3_out);
  not not_14 (not_14_out, nor_4_out);
  not not_15 (not_15_out, nor_1_out);
  not not_16 (not_16_out, nor_2_out);
  not not_17 (not_17_out, nand_1_out);
  not not_18 (not_18_out, nor_3_out);
  not not_19 (not_19_out, nand_1_out);
  not not_20 (not_20_out, nand_2_out);
  not not_21 (not_21_out, nor_4_out);
  not not_22 (not_22_out, nand_1_out);
  not not_23 (not_23_out, nand_2_out);
  not not_24 (not_24_out, nand_3_out);
  not not_25 (not_25_out, nand_1_out);
  not not_26 (not_26_out, nand_2_out);
  not not_27 (not_27_out, nand_3_out);
  not not_28 (not_28_out, nand_4_out);
  not not_29 (not_29_out, not_1_out);
  not not_30 (not_30_out, nor_1_out);
  not not_31 (not_31_out, nor_2_out);
  not not_32 (not_32_out, nor_3_out);
  not not_33 (not_33_out, nand_2_out);
  not not_34 (not_34_out, nor_4_out);
  not not_35 (not_35_out, nand_2_out);
  not not_36 (not_36_out, nand_3_out);
  not not_37 (not_37_out, nand_2_out);
  not not_38 (not_38_out, nand_3_out);
  not not_39 (not_39_out, nand_4_out);
  not not_40 (not_40_out, not_1_out);
  not not_41 (not_41_out, nor_2_out);
  not not_42 (not_42_out, nor_3_out);
  not not_43 (not_43_out, nor_4_out);
  not not_44 (not_44_out, nand_3_out);
  not not_45 (not_45_out, nand_3_out);
  not not_46 (not_46_out, nand_4_out);
  not not_47 (not_47_out, not_1_out);
  not not_48 (not_48_out, nor_3_out);
  not not_49 (not_49_out, nor_4_out);
  not not_50 (not_50_out, nand_4_out);
  not not_51 (not_51_out, not_1_out);
  not not_52 (not_52_out, nor_4_out);
  not not_53 (not_53_out, not_1_out);
  or or_1 (Gg, and_1_out, and_2_out, and_3_out, not_54_out);
  not not_54 (not_54_out, nand_1_out);
  or or_2 (or_2_out, not_16_out, not_17_out);
  or or_3 (or_3_out, not_18_out, not_19_out, not_20_out);
  or or_4 (or_4_out, not_21_out, not_22_out, not_23_out, not_24_out);
  or or_5 (or_5_out, not_25_out, not_26_out, not_27_out, not_28_out, not_29_out);
  and and_5 (and_5_out, nand_1_out, not_30_out);
  or or_6 (or_6_out, not_32_out, not_33_out);
  or or_7 (or_7_out, not_34_out, not_35_out, not_36_out);
  or or_8 (or_8_out, not_37_out, not_38_out, not_39_out, not_40_out);
  and and_6 (and_6_out, nand_2_out, not_41_out);
  or or_9 (or_9_out, not_43_out, not_44_out);
  or or_10 (or_10_out, not_45_out, not_46_out, not_47_out);
  and and_7 (and_7_out, nand_3_out, not_48_out);
  or or_11 (or_11_out, not_50_out, not_51_out);
  and and_8 (and_8_out, nand_4_out, not_52_out);
  and and_9 (C4, not_15_out, or_2_out, or_3_out, or_4_out, or_5_out);
  and and_10 (and_10_out, not_31_out, or_6_out, or_7_out, or_8_out);
  and and_11 (and_11_out, not_42_out, or_9_out, or_10_out);
  and and_12 (and_12_out, not_49_out, or_11_out);
  xor xor_1 (S3, and_5_out, and_10_out);
  xor xor_2 (S2, and_6_out, and_11_out);
  xor xor_3 (S1, and_7_out, and_12_out);
  xor xor_4 (S0, and_8_out, not_53_out);
endmodule

module \Gg和Pg  (
  input  X3,
  input  Y3,
  input  X2,
  input  Y2,
  input  X1,
  input  Y1,
  input  X0,
  input  Y0,
  input  C0,
  output C4,
  output C3,
  output C2,
  output C1,
  output Ps,
  output Gs
);

  wire and_1_out, and_2_out, and_3_out, and_4_out, and_5_out, and_6_out, and_7_out, and_8_out, and_9_out,
       and_10_out, and_12_out, and_13_out, and_14_out, G0_out, G1_out, G2_out, G3_out, P0_out, P1_out,
       P2_out, P3_out;

  and G3 (G3_out, X3, Y3);
  or P3 (P3_out, X3, Y3);
  and G2 (G2_out, X2, Y2);
  or P2 (P2_out, X2, Y2);
  and G1 (G1_out, X1, Y1);
  or P1 (P1_out, X1, Y1);
  and G0 (G0_out, X0, Y0);
  or P0 (P0_out, X0, Y0);
  and and_1 (and_1_out, P3_out, P2_out, P1_out, P0_out, C0);
  and and_2 (and_2_out, P3_out, P2_out, P1_out, G0_out);
  and and_3 (and_3_out, G1_out, P2_out, P3_out);
  and and_4 (and_4_out, P3_out, G2_out);
  and and_5 (and_5_out, P2_out, P1_out, P0_out, C0);
  and and_6 (and_6_out, P2_out, P1_out, G0_out);
  and and_7 (and_7_out, P2_out, G1_out);
  and and_8 (and_8_out, P1_out, P0_out, C0);
  and and_9 (and_9_out, P1_out, G0_out);
  and and_10 (and_10_out, P0_out, C0);
  and and_11 (Ps, P3_out, P2_out, P1_out, P0_out);
  and and_12 (and_12_out, P3_out, P2_out, P1_out, G0_out);
  and and_13 (and_13_out, P3_out, P2_out, G1_out);
  and and_14 (and_14_out, P3_out, G2_out);
  or or_1 (C4, and_1_out, and_2_out, G3_out, and_3_out, and_4_out);
  or or_2 (C3, and_5_out, G2_out, and_6_out, and_7_out);
  or or_3 (C2, G1_out, and_8_out, and_9_out);
  or or_4 (C1, G0_out, and_10_out);
  or or_5 (Gs, and_12_out, and_13_out, and_14_out, G3_out);
endmodule

module \_16位加法器  (
  input  C0,
  input  [15:0] A,
  input  [15:0] B,
  output Ps,
  output Gs,
  output [15:0] S,
  output C16
);

  wire \n4位加法器_1_c4 , \n4位加法器_1_gg , \n4位加法器_1_pg , \n4位加法器_2_c4 , \n4位加法器_2_gg , \n4位加法器_2_pg ,
       \n4位加法器_3_c4 , \n4位加法器_3_gg , \n4位加法器_3_pg , \n4位加法器_4_gg , \n4位加法器_4_pg ;

  \_4位加法器  \u_4位加法器_1  (
    .B3(B[3]), .A3(A[3]), .B2(B[2]), .A2(A[2]), .B1(B[1]), .A1(A[1]), .B0(B[0]), .A0(A[0]), .C0(C0),
    .C4(\n4位加法器_1_c4 ), .S3(S[3]), .S2(S[2]), .S1(S[1]), .S0(S[0]), .Gg(\n4位加法器_1_gg ), .Pg(\n4位加法器_1_pg ));
  \_4位加法器  \u_4位加法器_2  (
    .B3(B[7]), .A3(A[7]), .B2(B[6]), .A2(A[6]), .B1(B[5]), .A1(A[5]), .B0(B[4]), .A0(A[4]),
    .C0(\n4位加法器_1_c4 ), .C4(\n4位加法器_2_c4 ), .S3(S[7]), .S2(S[6]), .S1(S[5]), .S0(S[4]), .Gg(\n4位加法器_2_gg ),
    .Pg(\n4位加法器_2_pg ));
  \_4位加法器  \u_4位加法器_3  (
    .B3(B[11]), .A3(A[11]), .B2(B[10]), .A2(A[10]), .B1(B[9]), .A1(A[9]), .B0(B[8]), .A0(A[8]),
    .C0(\n4位加法器_2_c4 ), .C4(\n4位加法器_3_c4 ), .S3(S[11]), .S2(S[10]), .S1(S[9]), .S0(S[8]), .Gg(\n4位加法器_3_gg ),
    .Pg(\n4位加法器_3_pg ));
  \_4位加法器  \u_4位加法器_4  (
    .B3(B[15]), .A3(A[15]), .B2(B[14]), .A2(A[14]), .B1(B[13]), .A1(A[13]), .B0(B[12]), .A0(A[12]),
    .C0(\n4位加法器_3_c4 ), .C4(C16), .S3(S[15]), .S2(S[14]), .S1(S[13]), .S0(S[12]), .Gg(\n4位加法器_4_gg ),
    .Pg(\n4位加法器_4_pg ));
  \Gg和Pg  \gg和pg_1  (
    .X3(\n4位加法器_4_gg ), .Y3(\n4位加法器_4_pg ), .X2(\n4位加法器_3_gg ), .Y2(\n4位加法器_3_pg ), .X1(\n4位加法器_2_pg ),
    .Y1(\n4位加法器_2_gg ), .X0(\n4位加法器_1_pg ), .Y0(\n4位加法器_1_gg ), .C0(C0), .Ps(Ps), .Gs(Gs));  // open: C4, C3, C2, C1
endmodule

module \_32位加法器  (
  input  Cin,
  input  [31:0] A,
  input  [31:0] B,
  output [31:0] F,
  output Cout,
  output CF,
  output ZF,
  output SF,
  output OF
);

  wire and_1_out, and_2_out, and_3_out, and_4_out, \n16位加法器_1_c16 , not_1_out, not_2_out, not_3_out,
       not_4_out, not_5_out, not_6_out, or_1_out;

  \_16位加法器  \u_16位加法器_1  (.C0(Cin), .A(A[15:0]), .B(B[15:0]), .S(F[15:0]), .C16(\n16位加法器_1_c16 ));  // open: Ps, Gs
  \_16位加法器  \u_16位加法器_2  (.C0(\n16位加法器_1_c16 ), .A(A[31:16]), .B(B[31:16]), .S(F[31:16]), .C16(Cout));  // open: Ps, Gs
  xor xor_1 (CF, Cout, Cin);
  not not_1 (not_1_out, A[31]);
  not not_2 (not_2_out, B[31]);
  not not_3 (not_3_out, F[31]);
  not not_4 (not_4_out, B[31]);
  not not_5 (not_5_out, F[31]);
  not not_6 (not_6_out, A[31]);
  nor nor_1 (ZF, F[0], F[1], F[2], F[3], F[4], F[5], F[6], F[7], F[8], F[9], F[10], F[11], F[12], F[13], F[14], F[15], F[16], F[17], F[18], F[19], F[20], F[21], F[22], F[23], F[24], F[25], F[26], F[27], F[28], F[29], F[30], F[31]);
  and and_1 (and_1_out, F[31], A[31], B[31]);
  and and_2 (and_2_out, F[31], not_1_out, not_2_out);
  and and_3 (and_3_out, not_3_out, not_4_out, A[31]);
  and and_4 (and_4_out, not_5_out, B[31], not_6_out);
  or or_1 (or_1_out, and_1_out, and_2_out, and_3_out, and_4_out);
  xor xor_2 (OF, Cout, or_1_out);

  assign SF = F[31];
endmodule

module ALU (
  input  [31:0] A,
  input  [31:0] B,
  input  [3:0] ALUctr,
  output Zero,
  output [31:0] Result
);

  wire aluctr_1_sigctr, aluctr_1_subctr, multiplexer_2_out, \n32位加法器_1_cout , \n32位加法器_1_of , \n32位加法器_1_sf ,
       xor_2_out, xor_3_out;
  wire [1:0] aluctr_1_opctr;
  wire [31:0] bit_extender_1_out, bit_extender_2_out, \n32位加法器_1_f , or_1_out, xor_1_out;

  assign bit_extender_1_out = {{31{aluctr_1_subctr}}, aluctr_1_subctr};  // Bit_Extender bit_extender_1
  assign or_1_out = A | B;  // OR_Gate or_1, 32 bits wide
  assign xor_1_out = B ^ bit_extender_1_out;  // XOR_Gate xor_1, 32 bits wide
  \_32位加法器  \u_32位加法器_1  (
    .Cin(aluctr_1_subctr), .A(A), .B(xor_1_out), .F(\n32位加法器_1_f ), .Cout(\n32位加法器_1_cout ), .ZF(Zero),
    .SF(\n32位加法器_1_sf ), .OF(\n32位加法器_1_of ));  // open: CF
  Multiplexer #(.select(2), .width(32), .enable("false")) multiplexer_1 (
    .in0(\n32位加法器_1_f ), .in1(or_1_out), .in2(B), .in3(bit_extender_2_out), .out(Result), .sel(aluctr_1_opctr));
  ALUCtr aluctr_1 (.Cin(ALUctr), .SUBctr(aluctr_1_subctr), .SIGctr(aluctr_1_sigctr), .OPctr(aluctr_1_opctr));
  xor xor_2 (xor_2_out, aluctr_1_subctr, \n32位加法器_1_cout );
  xor xor_3 (xor_3_out, \n32位加法器_1_sf , \n32位加法器_1_of );
  Multiplexer #(.enable("false")) multiplexer_2 (
    .in0(xor_2_out), .in1(xor_3_out), .out(multiplexer_2_out), .sel(aluctr_1_sigctr));
  assign bit_extender_2_out = {{31{1'b0}}, multiplexer_2_out};  // Bit_Extender bit_extender_2
endmodule
